// Logisim project ALU_10_var_Final_Monika.circ as structural Verilog: 31 circuits, main circuit main
module main (
  input  [7:0] in_1,
  input  [7:0] in_2,
  input  [7:0] in_3,
  output [7:0] out_4,
  output ZF,
  output BAF,
  output BOF
);

  ALU_main alu_main_1 (.in_1(in_1), .in_2(in_2), .in_3(in_3), .out_4(out_4), .ZF(ZF), .BAF(BAF), .BOF(BOF));

  // Notes on the sheet:
  //   X
  //   Y
  //   OPCODE
  //   k=235
  //   Z
endmodule

// VLD
module Z235_VLD (
  input  [7:0] k,
  output Z,
  output ZF,
  output BAF,
  output BOF
);

  Comparator #(.mode("unsigned")) comparator_1 (.a(k), .b(8'heb), .lt(Z));  // open: gt, eq

  assign BAF = 1'b0;
  assign BOF = 1'b0;
  assign ZF = 1'b0;

  // Notes on the sheet:
  //   X
  //   VLD opcode: 00000001
endmodule

// ADD
module Z235_ADD (
  input  [7:0] in_1,
  input  [7:0] in_2,
  output [7:0] out_3,
  output ZF,
  output BAF,
  output BOF
);

  wire not_1_out, not_2_out, z235_vld_1_z, z235_vld_2_z;
  wire [0:0] adder_1_cout;
  wire [7:0] adder_1_out;

  Z235_VLD z235_vld_1 (.k(in_1), .Z(z235_vld_1_z));  // open: ZF, BAF, BOF
  Z235_VLD z235_vld_2 (.k(in_2), .Z(z235_vld_2_z));  // open: ZF, BAF, BOF
  Adder adder_1 (.a(in_1), .b(in_2), .out(adder_1_out), .cin(1'b0), .cout(adder_1_cout[0]));
  not not_1 (not_1_out, z235_vld_1_z);
  not not_2 (not_2_out, z235_vld_2_z);
  or or_1 (BAF, not_1_out, not_2_out);
  Divider divider_1 (.a(adder_1_out), .b(8'heb), .upper({{7{1'b0}}, adder_1_cout[0]}), .rem(out_3));  // open: out
  Comparator #(.mode("unsigned")) comparator_1 (.a(out_3), .b({8{1'b0}}), .eq(ZF));  // open: gt, lt

  assign BOF = 1'b0;

  // Notes on the sheet:
  //   X
  //   Y
  //   Z
  //   ADD opcode: 00010000
endmodule

// NEG
module Z235_NEG (
  input  [7:0] k,
  output [7:0] out_2,
  output ZF,
  output BAF,
  output BOF
);

  wire z235_vld_1_z;
  wire [7:0] subtractor_1_out;

  Subtractor subtractor_1 (.a(8'heb), .b(k), .out(subtractor_1_out), .bin(1'b0));  // open: bout
  Z235_VLD z235_vld_1 (.k(k), .Z(z235_vld_1_z));  // open: ZF, BAF, BOF
  Divider divider_1 (.a(subtractor_1_out), .b(8'heb), .rem(out_2));  // open: out, upper
  Comparator #(.mode("unsigned")) comparator_1 (.a(out_2), .b({8{1'b0}}), .eq(ZF));  // open: gt, lt
  not not_1 (BAF, z235_vld_1_z);

  assign BOF = 1'b0;

  // Notes on the sheet:
  //   X
  //   Z
  //   NEG opcode: 00000010
endmodule

// INC
module Z235_INC (
  input  [7:0] in_1,
  output [7:0] out_2,
  output ZF,
  output BAF,
  output BOF
);

  Z235_ADD z235_add_1 (.in_1(in_1), .in_2(8'h1), .out_3(out_2), .ZF(ZF), .BAF(BAF));  // open: BOF

  assign BOF = 1'b0;

  // Notes on the sheet:
  //   X
  //   Z
  //   INC opcode: 00000011
endmodule

// DEC
module Z235_DEC (
  input  [7:0] in_1,
  output [7:0] out_2,
  output ZF,
  output BAF,
  output BOF
);

  wire z235_vld_1_z;
  wire [7:0] z235_neg_1_out_2;

  Z235_NEG z235_neg_1 (.k(8'h1), .out_2(z235_neg_1_out_2));  // open: ZF, BAF, BOF
  Z235_VLD z235_vld_1 (.k(in_1), .Z(z235_vld_1_z));  // open: ZF, BAF, BOF
  Z235_ADD z235_add_1 (.in_1(in_1), .in_2(z235_neg_1_out_2), .out_3(out_2), .ZF(ZF));  // open: BAF, BOF
  not not_1 (BAF, z235_vld_1_z);

  assign BOF = 1'b0;

  // Notes on the sheet:
  //   Z
  //   DEC opcode: 00000100
endmodule

// CMPZ
module Z235_CMPZ (
  input  [7:0] in_1,
  output [7:0] out_2,
  output ZF,
  output BAF,
  output BOF
);

  Comparator #(.mode("unsigned")) comparator_1 (.a(in_1), .b({8{1'b0}}), .eq(out_2[0]));  // open: gt, lt

  assign BAF = 1'b0;
  assign BOF = 1'b0;
  assign out_2[7:1] = {7{1'b0}};
  assign ZF = out_2[0];

  // Notes on the sheet:
  //   X
  //   Z
  //   Z<-(X==0)
  //   BAF <- 0
  //   CMPZ opcode: 00000101
endmodule

// INV
module Z235_INV (
  input  [7:0] in_1,
  output [7:0] out_2,
  output ZF,
  output BAF,
  output BOF
);

  wire not_1_out, z235_cmpz_1_zf, z235_vld_1_z;

  Z235_VLD z235_vld_1 (.k(in_1), .Z(z235_vld_1_z));  // open: ZF, BAF, BOF
  ROM rom_1 (.addr(in_1), .data(out_2));  // open: sel
  not not_1 (not_1_out, z235_vld_1_z);
  Z235_CMPZ z235_cmpz_1 (.in_1(out_2), .ZF(z235_cmpz_1_zf));  // open: out_2, BAF, BOF
  or or_1 (BAF, z235_cmpz_1_zf, not_1_out);

  assign BOF = 1'b0;
  assign ZF = 1'b0;

  // Notes on the sheet:
  //   X
  //   contents of rom_1 (hex, n*v repeats v):
  //   0 1 76 9d 3b 0 c4 a8 93 d1 0 ab 62 d9 54 0 bf 53 de 63 0 38 cb 5c 31 0 e2 94 2a 9a 0 5b d5 39 9f 0
  //   6f 6c a7 e5 0 56 1c 52 db 0 2e 0 8e 18 0 6a 71 66 4a 0 15 21 4d 4 0 83 a3 61 e0 0 92 e4 c5 6d 0 60
  //   ad 84 36 0 c9 3a e8 77 0 ce 2b 11 e 0 29 d0 e3 a9 0 1f 17 bb 0 0 47 3f c 13 0 79 35 a2 ae 0 33 7b 25
  //   45 0 24 80 34 86 0 9c e9 2 4f 0 65 b7 6b c7 0 a6 c6 70 b8 0 3d 49 b6 72 0 d8 df ac a4 0 0 30 d4 cc 0
  //   42 8 1b c2 0 dd da c0 1d 0 74 3 b1 22 0 b5 67 3e 8b 0 7e 26 7 59 0 b 8a 48 68 0 e7 9e ca d6 0 a1 85
  //   7a 81 0 d3 5d 0 bd 0 10 99 cf 95 0 6 44 7f 7c 0 4c b2 16 90 0 51 c1 57 9 0 ba 8f 20 b3 0 88 d 98 2c
  //   0 97 12 89 40 0 1a 58 43 27 0 b0 4e 75 ea
  //   Z
  //   INV opcode: 00000110
endmodule

// SUB
module Z235_SUB (
  input  [7:0] in_1,
  input  [7:0] in_2,
  output [7:0] out_3,
  output ZF,
  output BAF,
  output BOF
);

  wire not_1_out, not_2_out, z235_vld_1_z, z235_vld_2_z;
  wire [7:0] z235_neg_1_out_2;

  Z235_NEG z235_neg_1 (.k(in_2), .out_2(z235_neg_1_out_2));  // open: ZF, BAF, BOF
  not not_1 (not_1_out, z235_vld_1_z);
  Z235_VLD z235_vld_1 (.k(in_1), .Z(z235_vld_1_z));  // open: ZF, BAF, BOF
  not not_2 (not_2_out, z235_vld_2_z);
  Z235_VLD z235_vld_2 (.k(in_2), .Z(z235_vld_2_z));  // open: ZF, BAF, BOF
  Z235_ADD z235_add_1 (.in_1(in_1), .in_2(z235_neg_1_out_2), .out_3(out_3), .ZF(ZF));  // open: BAF, BOF
  or or_1 (BAF, not_1_out, not_2_out);

  assign BOF = 1'b0;

  // Notes on the sheet:
  //   X
  //   Y
  //   Z
  //   SUB opcode: 00010001
endmodule

// MUL
module Z235_MUL (
  input  [7:0] in_1,
  input  [7:0] in_2,
  output [7:0] out_3,
  output ZF,
  output BAF,
  output BOF
);

  wire not_1_out, not_2_out, z235_vld_1_z, z235_vld_2_z;
  wire [7:0] multiplier_1_cout, multiplier_1_out;

  Z235_VLD z235_vld_1 (.k(in_1), .Z(z235_vld_1_z));  // open: ZF, BAF, BOF
  Z235_VLD z235_vld_2 (.k(in_2), .Z(z235_vld_2_z));  // open: ZF, BAF, BOF
  Multiplier multiplier_1 (.a(in_1), .b(in_2), .out(multiplier_1_out), .cin({8{1'b0}}), .cout(multiplier_1_cout));
  not not_1 (not_1_out, z235_vld_1_z);
  not not_2 (not_2_out, z235_vld_2_z);
  or or_1 (BAF, not_1_out, not_2_out);
  Divider divider_1 (.a(multiplier_1_out), .b(8'heb), .upper(multiplier_1_cout), .rem(out_3));  // open: out
  Comparator #(.mode("unsigned")) comparator_1 (.a(out_3), .b({8{1'b0}}), .eq(ZF));  // open: gt, lt

  assign BOF = 1'b0;

  // Notes on the sheet:
  //   X
  //   Y
  //   Z
  //   MUL opcode: 00010010
endmodule

// DIV
module Z235_DIV (
  input  [7:0] in_1,
  input  [7:0] in_2,
  output [7:0] out_3,
  output ZF,
  output BAF,
  output BOF
);

  wire not_1_out, not_2_out, not_3_out, z235_inv_1_baf, z235_mul_1_zf, z235_vld_1_z, z235_vld_2_z;
  wire [7:0] z235_inv_1_out_2;

  Z235_INV z235_inv_1 (.in_1(in_2), .out_2(z235_inv_1_out_2), .BAF(z235_inv_1_baf));  // open: ZF, BOF
  Z235_VLD z235_vld_1 (.k(in_2), .Z(z235_vld_1_z));  // open: ZF, BAF, BOF
  not not_1 (not_1_out, z235_vld_1_z);
  Z235_VLD z235_vld_2 (.k(in_1), .Z(z235_vld_2_z));  // open: ZF, BAF, BOF
  not not_2 (not_2_out, z235_vld_2_z);
  Z235_MUL z235_mul_1 (.in_1(in_1), .in_2(z235_inv_1_out_2), .out_3(out_3), .ZF(z235_mul_1_zf));  // open: BAF, BOF
  not not_3 (not_3_out, z235_inv_1_baf);
  or or_1 (BAF, z235_inv_1_baf, not_1_out, not_2_out);
  and and_1 (ZF, z235_mul_1_zf, not_3_out);

  assign BOF = 1'b0;

  // Notes on the sheet:
  //   X
  //   Y
  //   Z
  //   DIV opcode: 00010011
endmodule

// SHL
module Z235_SHL (
  input  [7:0] in_1,
  output [7:0] out_2,
  output ZF,
  output BAF,
  output BOF
);

  Shifter shifter_1 (.in(in_1), .\dist (3'b001), .out(out_2));
  Z235_CMPZ z235_cmpz_1 (.in_1(out_2), .ZF(ZF));  // open: out_2, BAF, BOF

  assign BAF = 1'b0;
  assign BOF = 1'b0;

  // Notes on the sheet:
  //   X
  //   Z
  //   SHL opcode: 00001000
endmodule

// SHR
module Z235_SHR (
  input  [7:0] in_1,
  output [7:0] out_2,
  output ZF,
  output BAF,
  output BOF
);

  Shifter #(.shift("lr")) shifter_1 (.in(in_1), .\dist (3'b001), .out(out_2));
  Z235_CMPZ z235_cmpz_1 (.in_1(out_2), .ZF(ZF));  // open: out_2, BAF, BOF

  assign BAF = 1'b0;
  assign BOF = 1'b0;

  // Notes on the sheet:
  //   X
  //   Z
  //   SHR opcode: 00001001
endmodule

// ROL
module Z235_ROL (
  input  [7:0] in_1,
  output [7:0] out_2,
  output ZF,
  output BAF,
  output BOF
);

  Shifter #(.shift("rl")) shifter_1 (.in(in_1), .\dist (3'b001), .out(out_2));
  Z235_CMPZ z235_cmpz_1 (.in_1(out_2), .ZF(ZF));  // open: out_2, BAF, BOF

  assign BAF = 1'b0;
  assign BOF = 1'b0;

  // Notes on the sheet:
  //   Z
  //   ROL opcode: 00001010
endmodule

// ROR
module Z235_ROR (
  input  [7:0] in_1,
  output [7:0] out_2,
  output ZF,
  output BAF,
  output BOF
);

  Shifter #(.shift("rr")) shifter_1 (.in(in_1), .\dist (3'b001), .out(out_2));
  Z235_CMPZ z235_cmpz_1 (.in_1(out_2), .ZF(ZF));  // open: out_2, BAF, BOF

  assign BAF = 1'b0;
  assign BOF = 1'b0;

  // Notes on the sheet:
  //   Z
  //   ROR opcode: 00001011
endmodule

// XOR
module Z235_XOR (
  input  [7:0] in_1,
  input  [7:0] in_2,
  output [7:0] out_3,
  output ZF,
  output BAF,
  output BOF
);

  xor xor_1 (out_3[6], in_1[6], in_2[6]);
  xor xor_2 (out_3[4], in_1[4], in_2[4]);
  xor xor_3 (out_3[2], in_1[2], in_2[2]);
  xor xor_4 (out_3[7], in_1[7], in_2[7]);
  xor xor_5 (out_3[5], in_1[5], in_2[5]);
  xor xor_6 (out_3[3], in_1[3], in_2[3]);
  xor xor_7 (out_3[1], in_1[1], in_2[1]);
  xor xor_8 (out_3[0], in_1[0], in_2[0]);
  Z235_CMPZ z235_cmpz_1 (.in_1(out_3), .ZF(ZF));  // open: out_2, BAF, BOF

  assign BAF = 1'b0;
  assign BOF = 1'b0;

  // Notes on the sheet:
  //   X
  //   Y
  //   XOR opcode: 00011100
  //   Z
endmodule

// AND
module Z235_AND (
  input  [7:0] in_1,
  input  [7:0] in_2,
  output [7:0] out_3,
  output ZF,
  output BAF,
  output BOF
);

  and and_1 (out_3[7], in_1[7], in_2[7]);
  and and_2 (out_3[6], in_1[6], in_2[6]);
  and and_3 (out_3[5], in_1[5], in_2[5]);
  and and_4 (out_3[4], in_1[4], in_2[4]);
  and and_5 (out_3[3], in_1[3], in_2[3]);
  and and_6 (out_3[2], in_1[2], in_2[2]);
  and and_7 (out_3[1], in_1[1], in_2[1]);
  and and_8 (out_3[0], in_1[0], in_2[0]);
  Z235_CMPZ z235_cmpz_1 (.in_1(out_3), .ZF(ZF));  // open: out_2, BAF, BOF

  assign BAF = 1'b0;
  assign BOF = 1'b0;

  // Notes on the sheet:
  //   X
  //   Y
  //   AND opcode: 00011101
  //   Z
endmodule

// OR
module Z235_OR (
  input  [7:0] in_1,
  input  [7:0] in_2,
  output [7:0] out_3,
  output ZF,
  output BAF,
  output BOF
);

  or or_1 (out_3[7], in_1[7], in_2[7]);
  or or_2 (out_3[6], in_1[6], in_2[6]);
  or or_3 (out_3[5], in_1[5], in_2[5]);
  or or_4 (out_3[4], in_1[4], in_2[4]);
  or or_5 (out_3[3], in_1[3], in_2[3]);
  or or_6 (out_3[2], in_1[2], in_2[2]);
  or or_7 (out_3[1], in_1[1], in_2[1]);
  or or_8 (out_3[0], in_1[0], in_2[0]);
  Z235_CMPZ z235_cmpz_1 (.in_1(out_3), .ZF(ZF));  // open: out_2, BAF, BOF

  assign BAF = 1'b0;
  assign BOF = 1'b0;

  // Notes on the sheet:
  //   X
  //   Y
  //   OR opcode: 00011110
  //   Z
endmodule

// NOT
module Z235_NOT (
  input  [7:0] in_1,
  output [7:0] out_2,
  output ZF,
  output BAF,
  output BOF
);

  assign out_2 = ~in_1;  // NOT_Gate not_1, 8 bits wide
  Z235_CMPZ z235_cmpz_1 (.in_1(out_2), .ZF(ZF));  // open: out_2, BAF, BOF

  assign BAF = 1'b0;
  assign BOF = 1'b0;

  // Notes on the sheet:
  //   Z
  //   NOT opcode: 00001100
endmodule

// N1
module Z235_N1 (
  input  [7:0] in_1,
  output [7:0] out_2,
  output ZF,
  output BAF,
  output BOF
);

  BitAdder bitadder_1 (.in0(in_1), .out(out_2[3:0]));
  Z235_CMPZ z235_cmpz_1 (.in_1({4'b0000, out_2[3:0]}), .ZF(ZF));  // open: out_2, BAF, BOF

  assign BAF = 1'b0;
  assign BOF = 1'b0;
  assign out_2[7:4] = 4'b0000;

  // Notes on the sheet:
  //   X
  //   Z
  //   N1 opcode: 00001101
endmodule

// N0
module Z235_N0 (
  input  [7:0] in_1,
  output [7:0] out_2,
  output ZF,
  output BAF,
  output BOF
);

  wire [3:0] bitadder_1_out;

  BitAdder bitadder_1 (.in0(in_1), .out(bitadder_1_out));
  Subtractor subtractor_1 (.a(8'h8), .b({4'b0000, bitadder_1_out}), .out(out_2), .bin(1'b0));  // open: bout
  Z235_CMPZ z235_cmpz_1 (.in_1(out_2), .ZF(ZF));  // open: out_2, BAF, BOF

  assign BAF = 1'b0;
  assign BOF = 1'b0;

  // Notes on the sheet:
  //   X
  //   Z
  //   N0 opcode: 00001110
endmodule

// OP1_5
module Z235_OP1_5 (
  input  [7:0] in_1,
  input  [7:0] in_2,
  output [7:0] out_3,
  output ZF,
  output BAF,
  output BOF
);

  Comparator #(.mode("unsigned")) comparator_1 (.a(in_1), .b(in_2), .lt(ZF));  // open: gt, eq
  not not_1 (out_3[0], ZF);

  assign BAF = 1'b0;
  assign BOF = 1'b0;
  assign out_3[7:1] = {7{1'b0}};

  // Notes on the sheet:
  //   X
  //   Y
  //   Z<- (X>=Y)
  //   operacija atliekama neatsižvelgiant į kūno struktūrą
  //   ZF<-(Z==0)
  //   Op1.5 opcode: 01011000
  //   Z
endmodule

// OP2_3
module Z235_OP2_3 (
  input  [7:0] in_1,
  input  [7:0] in_2,
  output [7:0] out_3,
  output ZF,
  output BAF,
  output BOF
);

  wire not_1_out, z235_neg_1_baf, z235_vld_1_z;
  wire [7:0] z235_neg_1_out_2;

  Z235_NEG z235_neg_1 (.k(in_2), .out_2(z235_neg_1_out_2), .BAF(z235_neg_1_baf));  // open: ZF, BOF
  not not_1 (not_1_out, z235_vld_1_z);
  Z235_VLD z235_vld_1 (.k(in_1), .Z(z235_vld_1_z));  // open: ZF, BAF, BOF
  Comparator #(.mode("unsigned")) comparator_1 (.a(in_1), .b(z235_neg_1_out_2), .eq(out_3[0]));  // open: gt, lt
  or or_1 (BAF, z235_neg_1_baf, not_1_out);
  not not_2 (ZF, out_3[0]);

  assign BOF = 1'b0;
  assign out_3[7:1] = {7{1'b0}};

  // Notes on the sheet:
  //   X
  //   Y
  //   Z<- (X==NEG Y)
  //   ZF<-(Z==0)
  //   Z
  //   Op2.3 opcode: 01011001
endmodule

// OP3_7
module Z235_OP3_7 (
  input  [7:0] in_1,
  output [7:0] out_2,
  output ZF,
  output BAF,
  output BOF
);

  wire z235_vld_1_z;

  Z235_VLD z235_vld_1 (.k(in_1), .Z(z235_vld_1_z));  // open: ZF, BAF, BOF
  ROM rom_1 (.addr(in_1), .data(out_2));  // open: sel
  not not_1 (BAF, z235_vld_1_z);

  assign BOF = 1'b0;
  assign ZF = 1'b0;

  // Notes on the sheet:
  //   X
  //   Z<-(X^(1/5))
  //   contents of rom_1 (hex, n*v repeats v):
  //   0 1 7a 6c 4f 14 10 de 3 95 5a 1a 48 da 3b 2d 83 c5 53 86 aa 6 75 c1 59 a5 29 70 94 c7 55 97 2 df 40
  //   d2 15 c0 85 2c 3c 1f 1b cb ae a0 2e 2f 30 a9 9b 7e 43 3f 22 32 c4 89 49 77 1e 6a 5c b2 9 82 b5 d9 35
  //   a4 5 88 d4 58 9f c3 b 84 c6 31 23 6f 16 44 4 b4 5b 6b 4e 4a f dd cf 5d 5e 5f d8 ca ad 72 6e 51 61 8
  //   b8 78 a6 4d 99 8b e1 38 b1 e4 1d 64 d3 34 b7 18 87 ce 7 3a b3 a 60 52 9e 45 73 33 e3 8a 9a 7d 79 3e
  //   21 13 8c 8d 8e 1c e dc a1 9d 80 90 37 e7 a7 d5 7c c8 ba 25 67 e0 28 4c 93 17 63 e6 47 b6 12 36 69 e2
  //   39 8f 81 cd 74 a2 62 27 b9 c9 ac a8 6d 50 42 bb bc bd 4b 3d 20 d0 cc af bf 66 2b d6 19 ab c e9 54 96
  //   24 57 7b c2 46 92 2a 76 e5 41 65 98 26 68 be b0 11 a3 d1 91 56 e8 d db d7 9c 7f 71 ea
  //   ZF <- 0
  //   Z
  //   OP3.7 opcode: 01011010
endmodule

// ALU
module ALU_main (
  input  [7:0] in_1,
  input  [7:0] in_2,
  input  [7:0] in_3,
  output [7:0] out_4,
  output ZF,
  output BAF,
  output BOF
);

  wire [4:0] rom_1_data;
  wire [10:0] ADD, AND, CMPZ, DEC, DIV, INC, INV, MUL, N0, N1, NEG, NOT, OP1, OP2, OP3, OR, ROL, ROR, SHL,
       SHR, SUB, VLD, XOR;

  Z235_VLD z235_vld_1 (.k(in_1), .Z(VLD[0]), .ZF(VLD[8]), .BAF(VLD[9]), .BOF(VLD[10]));
  Z235_ADD z235_add_1 (.in_1(in_1), .in_2(in_2), .out_3(ADD[7:0]), .ZF(ADD[8]), .BAF(ADD[9]), .BOF(ADD[10]));
  Z235_NEG z235_neg_1 (.k(in_1), .out_2(NEG[7:0]), .ZF(NEG[8]), .BAF(NEG[9]), .BOF(NEG[10]));
  Z235_INC z235_inc_1 (.in_1(in_1), .out_2(INC[7:0]), .ZF(INC[8]), .BAF(INC[9]), .BOF(INC[10]));
  Z235_DEC z235_dec_1 (.in_1(in_1), .out_2(DEC[7:0]), .ZF(DEC[8]), .BAF(DEC[9]), .BOF(DEC[10]));
  Z235_CMPZ z235_cmpz_1 (.in_1(in_1), .out_2(CMPZ[7:0]), .ZF(CMPZ[8]), .BAF(CMPZ[9]), .BOF(CMPZ[10]));
  Z235_INV z235_inv_1 (.in_1(in_1), .out_2(INV[7:0]), .ZF(INV[8]), .BAF(INV[9]), .BOF(INV[10]));
  Z235_SUB z235_sub_1 (.in_1(in_1), .in_2(in_2), .out_3(SUB[7:0]), .ZF(SUB[8]), .BAF(SUB[9]), .BOF(SUB[10]));
  Z235_MUL z235_mul_1 (.in_1(in_1), .in_2(in_2), .out_3(MUL[7:0]), .ZF(MUL[8]), .BAF(MUL[9]), .BOF(MUL[10]));
  Z235_DIV z235_div_1 (.in_1(in_1), .in_2(in_2), .out_3(DIV[7:0]), .ZF(DIV[8]), .BAF(DIV[9]), .BOF(DIV[10]));
  Z235_SHL z235_shl_1 (.in_1(in_1), .out_2(SHL[7:0]), .ZF(SHL[8]), .BAF(SHL[9]), .BOF(SHL[10]));
  Z235_SHR z235_shr_1 (.in_1(in_1), .out_2(SHR[7:0]), .ZF(SHR[8]), .BAF(SHR[9]), .BOF(SHR[10]));
  Z235_ROL z235_rol_1 (.in_1(in_1), .out_2(ROL[7:0]), .ZF(ROL[8]), .BAF(ROL[9]), .BOF(ROL[10]));
  Z235_ROR z235_ror_1 (.in_1(in_1), .out_2(ROR[7:0]), .ZF(ROR[8]), .BAF(ROR[9]), .BOF(ROR[10]));
  Z235_XOR z235_xor_1 (.in_1(in_1), .in_2(in_2), .out_3(XOR[7:0]), .ZF(XOR[8]), .BAF(XOR[9]), .BOF(XOR[10]));
  Z235_AND z235_and_1 (.in_1(in_1), .in_2(in_2), .out_3(AND[7:0]), .ZF(AND[8]), .BAF(AND[9]), .BOF(AND[10]));
  Z235_OR z235_or_1 (.in_1(in_1), .in_2(in_2), .out_3(OR[7:0]), .ZF(OR[8]), .BAF(OR[9]), .BOF(OR[10]));
  Z235_NOT z235_not_1 (.in_1(in_1), .out_2(NOT[7:0]), .ZF(NOT[8]), .BAF(NOT[9]), .BOF(NOT[10]));
  Z235_N1 z235_n1_1 (.in_1(in_1), .out_2(N1[7:0]), .ZF(N1[8]), .BAF(N1[9]), .BOF(N1[10]));
  Z235_N0 z235_n0_1 (.in_1(in_1), .out_2(N0[7:0]), .ZF(N0[8]), .BAF(N0[9]), .BOF(N0[10]));
  Z235_OP1_5 z235_op1_5_1 (.in_1(in_1), .in_2(in_2), .out_3(OP1[7:0]), .ZF(OP1[8]), .BAF(OP1[9]), .BOF(OP1[10]));
  Z235_OP2_3 z235_op2_3_1 (.in_1(in_1), .in_2(in_2), .out_3(OP2[7:0]), .ZF(OP2[8]), .BAF(OP2[9]), .BOF(OP2[10]));
  Z235_OP3_7 z235_op3_7_1 (.in_1(in_1), .out_2(OP3[7:0]), .ZF(OP3[8]), .BAF(OP3[9]), .BOF(OP3[10]));
  ROM #(.dataWidth(5)) rom_1 (.addr(in_3), .data(rom_1_data));  // open: sel
  Multiplexer #(.select(5), .width(11), .enable("false")) multiplexer_1 (
    .in0(11'h400), .in1({VLD[10:8], {7{1'b0}}, VLD[0]}), .in2(ADD), .in3(NEG), .in4(INC), .in5(DEC),
    .in6(CMPZ), .in7(INV), .in8(SUB), .in9(MUL), .in10(DIV), .in11(SHL), .in12(SHR), .in13(ROL), .in14(ROR),
    .in15(XOR), .in16(AND), .in17(OR), .in18(NOT), .in19(N1), .in20(N0), .in21(OP1), .in22(OP2), .in23(OP3),
    .out({BOF, BAF, ZF, out_4}), .sel(rom_1_data));  // open: in24, in25, in26, in27, in28, in29, in30, in31

  // Notes on the sheet:
  //   operacijos, kurios nepriklauso nuo žiedo, turi BAF <-0
  //   X
  //   Y
  //   OPCODE
  //   contents of rom_1 (hex, n*v repeats v):
  //   0 1 3 4 5 6 7 0 b c d e 12 13 14 0 2 8 9 a 8*0 f 10 11 57*0 15 16 17
  //   11 bitas: bof, 10 bitas baf, 9 bitas: ZF, like 8 Z 
  //   Z
endmodule

module Z235_ax_5_x_b_0 (
  input  [7:0] in_1,
  input  [7:0] in_2,
  output [7:0] out_3,
  output [7:0] out_4,
  output ZF,
  output BAF
);

  wire not_1_out, not_2_out, z235_vld_1_z, z235_vld_2_z;
  wire [7:0] z235_neg_1_out_2;

  Z235_VLD z235_vld_1 (.k(in_2), .Z(z235_vld_1_z));  // open: ZF, BAF, BOF
  Z235_VLD z235_vld_2 (.k(in_1), .Z(z235_vld_2_z));  // open: ZF, BAF, BOF
  not not_1 (not_1_out, z235_vld_1_z);
  not not_2 (not_2_out, z235_vld_2_z);
  Z235_NEG z235_neg_1 (.k(in_2), .out_2(z235_neg_1_out_2));  // open: ZF, BAF, BOF
  or or_1 (BAF, not_1_out, not_2_out);
  Comparator #(.mode("unsigned")) comparator_1 (.a(z235_neg_1_out_2), .b({8{1'b0}}), .eq(ZF));  // open: gt, lt
  Z235_MUL z235_mul_1 (.in_1(in_1), .in_2(z235_neg_1_out_2), .out_3(out_3));  // open: ZF, BAF, BOF
  Z235_OP3_7 z235_op3_7_1 (.in_1(out_3), .out_2(out_4));  // open: ZF, BAF, BOF

  // Notes on the sheet:
  //   X(a)
  //   Y(b)
endmodule

// X^5
module _235_X_5 (
  input  [7:0] in_1,
  input  [7:0] in_2,
  output [7:0] out_3,
  output BAF
);

  wire z235_vld_1_z;
  wire [7:0] z235_mul_1_out_3, z235_mul_2_out_3, z235_mul_3_out_3, z235_mul_4_out_3;

  Z235_MUL z235_mul_1 (.in_1(in_2), .in_2(in_2), .out_3(z235_mul_1_out_3));  // open: ZF, BAF, BOF
  Z235_MUL z235_mul_2 (.in_1(z235_mul_1_out_3), .in_2(in_2), .out_3(z235_mul_2_out_3));  // open: ZF, BAF, BOF
  Z235_VLD z235_vld_1 (.k(in_2), .Z(z235_vld_1_z));  // open: ZF, BAF, BOF
  Z235_MUL z235_mul_3 (.in_1(z235_mul_2_out_3), .in_2(in_2), .out_3(z235_mul_3_out_3));  // open: ZF, BAF, BOF
  not not_1 (BAF, z235_vld_1_z);
  Z235_MUL z235_mul_4 (.in_1(z235_mul_3_out_3), .in_2(in_2), .out_3(z235_mul_4_out_3));  // open: ZF, BAF, BOF
  Z235_MUL z235_mul_5 (.in_1(in_1), .in_2(z235_mul_4_out_3), .out_3(out_3));  // open: ZF, BAF, BOF

  // Notes on the sheet:
  //   X(a)
  //   X
endmodule

module Inv_5 (
  input  [7:0] in_1,
  output [7:0] out_2,
  output ZF,
  output BAF,
  output BOF
);

  wire not_1_out, z235_cmpz_1_zf, z235_vld_1_z;

  Z235_VLD z235_vld_1 (.k(in_1), .Z(z235_vld_1_z));  // open: ZF, BAF, BOF
  ROM rom_1 (.addr(in_1), .data(out_2));  // open: sel
  not not_1 (not_1_out, z235_vld_1_z);
  Z235_CMPZ z235_cmpz_1 (.in_1(out_2), .ZF(z235_cmpz_1_zf));  // open: out_2, BAF, BOF
  or or_1 (BAF, z235_cmpz_1_zf, not_1_out);

  assign BOF = 1'b0;
  assign ZF = 1'b0;

  // Notes on the sheet:
  //   X
  //   contents of rom_1 (hex, n*v repeats v):
  //   0 1 3 2 4
  //   Z
endmodule

module Inv_47 (
  input  [7:0] in_1,
  output [7:0] out_2,
  output ZF,
  output BAF,
  output BOF
);

  wire not_1_out, z235_cmpz_1_zf, z235_vld_1_z;

  Z235_VLD z235_vld_1 (.k(in_1), .Z(z235_vld_1_z));  // open: ZF, BAF, BOF
  ROM rom_1 (.addr(in_1), .data(out_2));  // open: sel
  not not_1 (not_1_out, z235_vld_1_z);
  Z235_CMPZ z235_cmpz_1 (.in_1(out_2), .ZF(z235_cmpz_1_zf));  // open: out_2, BAF, BOF
  or or_1 (BAF, z235_cmpz_1_zf, not_1_out);

  assign BOF = 1'b0;
  assign ZF = 1'b0;

  // Notes on the sheet:
  //   X
  //   contents of rom_1 (hex, n*v repeats v):
  //   0 1 18 10 c 13 8 1b 6 15 21 1e 4 1d 25 16 3 24 22 5 28 9 f 2d 2 20 26 7 2a d b 2c 19 a 12 2b 11 e 1a
  //   29 14 27 1c 23 1f 17 2e
  //   Z
endmodule

module LygtisMod5 (
  input  [7:0] in_1,
  input  [7:0] in_2,
  output [7:0] out_3
);

  wire [7:0] divider_1_rem, divider_2_rem;

  Divider divider_1 (.a(in_1), .b(8'h5), .rem(divider_1_rem));  // open: out, upper
  Divider divider_2 (.a(in_2), .b(8'h5), .rem(divider_2_rem));  // open: out, upper
  ROM rom_1 (.addr({divider_1_rem[3:0], divider_2_rem[3:0]}), .data(out_3));  // open: sel

  // Notes on the sheet:
  //   X(a)
  //   Y(b)
  //   contents of rom_1 (hex, n*v repeats v):
  //   0 4 3 2 1 12*0 2 4 1 3 12*0 3 1 4 2 12*0 1 2 3 4
endmodule

module Lygtis_mod47 (
  input  [7:0] in_1,
  input  [7:0] in_2
);

  wire [7:0] divider_1_rem, divider_2_rem;

  Divider divider_1 (.a(in_1), .b(8'h2f), .rem(divider_1_rem));  // open: out, upper
  Divider divider_2 (.a(in_2), .b(8'h2f), .rem(divider_2_rem));  // open: out, upper

  // Notes on the sheet:
  //   X(a)
  //   Y(b)
endmodule
