// Logisim project F131-ALU.circ as structural Verilog: 22 circuits, main circuit main
module main (
  input  [4:0] OpCode,
  input  [7:0] x,
  input  [7:0] y,
  output [7:0] Z,
  output ZF,
  output BAF
);

  wire [0:0] f131_cmpz_1_zf, f131_vld_1_out_2;
  wire [7:0] f131_add_1_z, f131_and_1_out_3, f131_dec_1_out_2, f131_inc_1_out_2, f131_mul_1_z,
       f131_n0_1_out_2, f131_n1_1_out_2, f131_neg_1_out_2, f131_not_1_out_2, f131_or_1_out_3,
       f131_rol_1_out_2, f131_ror_1_out_2, f131_shl_1_out_2, f131_shr_1_out_2, f131_sub_1_out_3,
       f131_xor_1_out_3;
  wire [8:8] f131_n0_1_zf;
  wire [9:0] f131_op1_1_z, f131_op2_1_z;
  wire [9:8] f131_add_1_baf, f131_and_1_zf, f131_dec_1_zf, f131_inc_1_zf, f131_mul_1_zf, f131_n1_1_zf,
       f131_neg_1_zf, f131_not_1_zf, f131_or_1_zf, f131_rol_1_zf, f131_ror_1_zf, f131_shl_1_zf,
       f131_shr_1_zf, f131_sub_1_zf, f131_xor_1_zf;

  F131_ADD f131_add_1 (.x(x), .y(y), .Z(f131_add_1_z), .ZF(f131_add_1_baf[9]), .BAF(f131_add_1_baf[8]));
  F131_VLD f131_vld_1 (.in_1(x), .out_2(f131_vld_1_out_2[0]));
  F131_NEG f131_neg_1 (.in_1(x), .out_2(f131_neg_1_out_2), .ZF(f131_neg_1_zf[8]), .BAF(f131_neg_1_zf[9]));
  F131_CMPZ f131_cmpz_1 (.in_1(x), .ZF(f131_cmpz_1_zf[0]));
  F131_INC f131_inc_1 (.in_1(x), .out_2(f131_inc_1_out_2), .ZF(f131_inc_1_zf[8]), .BAF(f131_inc_1_zf[9]));
  F131_SUB f131_sub_1 (.in_1(x), .in_2(y), .out_3(f131_sub_1_out_3), .ZF(f131_sub_1_zf[8]), .BAF(f131_sub_1_zf[9]));
  F131_DEC f131_dec_1 (.in_1(x), .out_2(f131_dec_1_out_2), .ZF(f131_dec_1_zf[8]), .BAF(f131_dec_1_zf[9]));
  F131_MUL f131_mul_1 (.x(x), .y(y), .Z(f131_mul_1_z), .ZF(f131_mul_1_zf[8]), .BAF(f131_mul_1_zf[9]));
  F131_DIV f131_div_1 ();  // open: in_1, in_2
  F131_SHL f131_shl_1 (.in_1(x), .out_2(f131_shl_1_out_2), .ZF(f131_shl_1_zf[8]), .BAF(f131_shl_1_zf[9]));
  F131_SHR f131_shr_1 (.in_1(x), .out_2(f131_shr_1_out_2), .ZF(f131_shr_1_zf[8]), .BAF(f131_shr_1_zf[9]));
  F131_ROL f131_rol_1 (.in_1(x), .out_2(f131_rol_1_out_2), .ZF(f131_rol_1_zf[8]), .BAF(f131_rol_1_zf[9]));
  F131_ROR f131_ror_1 (.in_1(x), .out_2(f131_ror_1_out_2), .ZF(f131_ror_1_zf[8]), .BAF(f131_ror_1_zf[9]));
  F131_XOR f131_xor_1 (.in_1(x), .in_2(y), .out_3(f131_xor_1_out_3), .ZF(f131_xor_1_zf[8]), .BAF(f131_xor_1_zf[9]));
  F131_AND f131_and_1 (.in_1(x), .in_2(y), .out_3(f131_and_1_out_3), .ZF(f131_and_1_zf[8]), .BAF(f131_and_1_zf[9]));
  F131_OR f131_or_1 (.in_1(x), .in_2(y), .out_3(f131_or_1_out_3), .ZF(f131_or_1_zf[8]), .BAF(f131_or_1_zf[9]));
  F131_NOT f131_not_1 (.in_1(x), .out_2(f131_not_1_out_2), .ZF(f131_not_1_zf[8]), .BAF(f131_not_1_zf[9]));
  F131_N1 f131_n1_1 (.in_1(x), .out_2(f131_n1_1_out_2), .ZF(f131_n1_1_zf[8]), .BAF(f131_n1_1_zf[9]));
  F131_N0 f131_n0_1 (.in_1(x), .out_2(f131_n0_1_out_2), .ZF(f131_n0_1_zf[8]));
  F131_OP1 f131_op1_1 (.in_1(x), .in_2(y), .Z(f131_op1_1_z[0]), .ZF(f131_op1_1_z[8]), .BAF(f131_op1_1_z[9]));
  F131_OP2 f131_op2_1 (.in_1(x), .in_2(y), .Z(f131_op2_1_z[0]), .ZF(f131_op2_1_z[8]), .BAF(f131_op2_1_z[9]));
  Multiplexer #(.select(5), .width(10)) multiplexer_1 (
    .in0({f131_add_1_baf, f131_add_1_z}), .in1({{9{1'b0}}, f131_vld_1_out_2[0]}),
    .in2({f131_neg_1_zf, f131_neg_1_out_2}), .in3({{9{1'b0}}, f131_cmpz_1_zf[0]}),
    .in4({f131_inc_1_zf, f131_inc_1_out_2}), .in5({f131_sub_1_zf, f131_sub_1_out_3}),
    .in6({f131_dec_1_zf, f131_dec_1_out_2}), .in7({f131_mul_1_zf, f131_mul_1_z}), .in8({10{1'b0}}),
    .in9({f131_shl_1_zf, f131_shl_1_out_2}), .in10({f131_shr_1_zf, f131_shr_1_out_2}),
    .in11({f131_rol_1_zf, f131_rol_1_out_2}), .in12({f131_ror_1_zf, f131_ror_1_out_2}),
    .in13({f131_xor_1_zf, f131_xor_1_out_3}), .in14({f131_and_1_zf, f131_and_1_out_3}),
    .in15({f131_or_1_zf, f131_or_1_out_3}), .in16({f131_not_1_zf, f131_not_1_out_2}),
    .in17({f131_n1_1_zf, f131_n1_1_out_2}), .in18({1'b0, f131_n0_1_zf[8], f131_n0_1_out_2}),
    .in19({f131_op1_1_z[9:8], {7{1'b0}}, f131_op1_1_z[0]}), .out({BAF, ZF, Z}), .sel(OpCode), .en(1'b1));  // open: in20, in21, in22, in23, in24, in25, in26, in27, in28, in29, in30, in31

  // Other names for the same wires on the sheet: OPC_IN[4:0] = OpCode

  // Notes on the sheet:
  //   MISSING OPS: 
  //   DIV
  //   INV
  //   OP3
  //   TODO:
  //   Add BOF
  //   Fix incorrect ZF and BAF
  //   Expand multiplex with ROM
  //   fix
  //   TODO
  //   fix
endmodule

// ADD
module F131_ADD (
  input  [7:0] x,
  input  [7:0] y,
  output [7:0] Z,
  output ZF,
  output BAF
);

  wire comparator_1_lt, comparator_2_lt, not_1_out, not_2_out;
  wire [7:0] adder_1_out;
  wire [8:8] adder_1_cout, divider_1_rem;

  Adder adder_1 (.a(x), .b(y), .out(adder_1_out), .cin(1'b0), .cout(adder_1_cout[8]));
  Divider #(.width(9)) divider_1 (
    .a({adder_1_cout[8], adder_1_out}), .b(9'h83), .upper({9{1'b0}}), .rem({divider_1_rem[8], Z}));  // open: out
  Comparator #(.mode("unsigned")) comparator_1 (.a(x), .b(8'h83), .lt(comparator_1_lt));  // open: gt, eq
  not not_1 (not_1_out, comparator_1_lt);
  not not_2 (not_2_out, comparator_2_lt);
  Comparator #(.mode("unsigned")) comparator_2 (.a(y), .b(8'h83), .lt(comparator_2_lt));  // open: gt, eq
  or or_1 (BAF, not_1_out, not_2_out);
  F131_CMPZ f131_cmpz_1 (.in_1(Z), .ZF(ZF));

  // Notes on the sheet:
  //   x+y -> (F131) -> (x+y) % 131
endmodule

// VLD
module F131_VLD (
  input  [7:0] in_1,
  output out_2
);

  Comparator #(.mode("unsigned")) comparator_1 (.a(in_1), .b(8'h83), .lt(out_2));  // open: gt, eq
endmodule

// NEG
module F131_NEG (
  input  [7:0] in_1,
  output [7:0] out_2,
  output ZF,
  output BAF
);

  wire f131_vld_1_out_2, not_1_out;
  wire [7:0] subtractor_1_out;

  assign out_2 = not_1_out ? subtractor_1_out : 8'bz;  // Controlled_Buffer controlled_buffer_1
  Subtractor subtractor_1 (.a(8'h83), .b(in_1), .out(subtractor_1_out));  // open: bin, bout
  not not_1 (not_1_out, ZF);
  Comparator comparator_1 (.a(in_1), .b({8{1'b0}}), .eq(ZF));  // open: gt, lt
  F131_VLD f131_vld_1 (.in_1(in_1), .out_2(f131_vld_1_out_2));
  assign out_2 = ZF ? in_1 : 8'bz;  // Controlled_Buffer controlled_buffer_2
  not not_2 (BAF, f131_vld_1_out_2);
endmodule

// CMPZ
module F131_CMPZ (
  input  [7:0] in_1,
  output ZF
);

  Comparator #(.mode("unsigned")) comparator_1 (.a(in_1), .b({8{1'b0}}), .eq(ZF));  // open: gt, lt
endmodule

// INC
module F131_INC (
  input  [7:0] in_1,
  output [7:0] out_2,
  output ZF,
  output BAF
);

  F131_ADD f131_add_1 (.x(in_1), .y(8'h1), .Z(out_2), .ZF(ZF), .BAF(BAF));
endmodule

// SUB
module F131_SUB (
  input  [7:0] in_1,
  input  [7:0] in_2,
  output [7:0] out_3,
  output ZF,
  output BAF
);

  wire f131_add_1_baf, f131_neg_1_baf;
  wire [7:0] f131_neg_1_out_2;

  F131_ADD f131_add_1 (.x(in_1), .y(f131_neg_1_out_2), .Z(out_3), .ZF(ZF), .BAF(f131_add_1_baf));
  F131_NEG f131_neg_1 (.in_1(in_2), .out_2(f131_neg_1_out_2), .BAF(f131_neg_1_baf));  // open: ZF
  or or_1 (BAF, f131_add_1_baf, f131_neg_1_baf);
endmodule

// DEC
module F131_DEC (
  input  [7:0] in_1,
  output [7:0] out_2,
  output ZF,
  output BAF
);

  F131_SUB f131_sub_1 (.in_1(in_1), .in_2(8'h1), .out_3(out_2), .ZF(ZF), .BAF(BAF));
endmodule

// MUL
module F131_MUL (
  input  [7:0] x,
  input  [7:0] y,
  output [7:0] Z,
  output ZF,
  output BAF
);

  wire comparator_1_eq, comparator_2_eq;
  wire [7:0] C1, multiplier_1_out;

  Multiplier multiplier_1 (.a(x), .b(y), .out(multiplier_1_out), .cin({8{1'b0}}), .cout(C1));
  Comparator #(.mode("unsigned")) comparator_1 (.a(x), .b(8'h83), .eq(comparator_1_eq));  // open: gt, lt
  Comparator #(.mode("unsigned")) comparator_2 (.a(y), .b(8'h83), .eq(comparator_2_eq));  // open: gt, lt
  Divider divider_1 (.a(multiplier_1_out), .b(8'h83), .upper(C1), .rem(Z));  // open: out
  or or_1 (BAF, comparator_1_eq, comparator_2_eq);
  F131_CMPZ f131_cmpz_1 (.in_1(Z), .ZF(ZF));
endmodule

// DIV
module F131_DIV (
  input  [7:0] in_1,
  input  [7:0] in_2
);
endmodule

// SHL
module F131_SHL (
  input  [7:0] in_1,
  output [7:0] out_2,
  output ZF,
  output BAF
);

  wire f131_vld_1_out_2;

  F131_VLD f131_vld_1 (.in_1(in_1), .out_2(f131_vld_1_out_2));
  Shifter shifter_1 (.in(in_1), .\dist (3'b001), .out(out_2));
  not not_1 (BAF, f131_vld_1_out_2);
  F131_CMPZ f131_cmpz_1 (.in_1(out_2), .ZF(ZF));
endmodule

// SHR
module F131_SHR (
  input  [7:0] in_1,
  output [7:0] out_2,
  output ZF,
  output BAF
);

  wire f131_vld_1_out_2;

  F131_VLD f131_vld_1 (.in_1(in_1), .out_2(f131_vld_1_out_2));
  Shifter #(.shift("lr")) shifter_1 (.in(in_1), .\dist (3'b001), .out(out_2));
  not not_1 (BAF, f131_vld_1_out_2);
  F131_CMPZ f131_cmpz_1 (.in_1(out_2), .ZF(ZF));
endmodule

// ROL
module F131_ROL (
  input  [7:0] in_1,
  output [7:0] out_2,
  output ZF,
  output BAF
);

  wire f131_vld_1_out_2;

  F131_VLD f131_vld_1 (.in_1(in_1), .out_2(f131_vld_1_out_2));
  Shifter #(.shift("rl")) shifter_1 (.in(in_1), .\dist (3'b001), .out(out_2));
  not not_1 (BAF, f131_vld_1_out_2);
  F131_CMPZ f131_cmpz_1 (.in_1(out_2), .ZF(ZF));
endmodule

// ROR
module F131_ROR (
  input  [7:0] in_1,
  output [7:0] out_2,
  output ZF,
  output BAF
);

  wire f131_vld_1_out_2;

  F131_VLD f131_vld_1 (.in_1(in_1), .out_2(f131_vld_1_out_2));
  Shifter #(.shift("rr")) shifter_1 (.in(in_1), .\dist (3'b001), .out(out_2));
  not not_1 (BAF, f131_vld_1_out_2);
  F131_CMPZ f131_cmpz_1 (.in_1(out_2), .ZF(ZF));
endmodule

// XOR
module F131_XOR (
  input  [7:0] in_1,
  input  [7:0] in_2,
  output [7:0] out_3,
  output ZF,
  output BAF
);

  wire f131_vld_1_out_2, f131_vld_2_out_2, not_1_out, not_2_out;

  assign out_3 = in_1 ^ in_2;  // XOR_Gate xor_1, 8 bits wide
  F131_VLD f131_vld_1 (.in_1(in_1), .out_2(f131_vld_1_out_2));
  F131_VLD f131_vld_2 (.in_1(in_2), .out_2(f131_vld_2_out_2));
  F131_CMPZ f131_cmpz_1 (.in_1(out_3), .ZF(ZF));
  not not_1 (not_1_out, f131_vld_1_out_2);
  not not_2 (not_2_out, f131_vld_2_out_2);
  or or_1 (BAF, not_1_out, not_2_out);
endmodule

// AND
module F131_AND (
  input  [7:0] in_1,
  input  [7:0] in_2,
  output [7:0] out_3,
  output ZF,
  output BAF
);

  wire f131_vld_1_out_2, f131_vld_2_out_2, not_1_out, not_2_out;

  assign out_3 = in_1 & in_2;  // AND_Gate and_1, 8 bits wide
  F131_VLD f131_vld_1 (.in_1(in_1), .out_2(f131_vld_1_out_2));
  F131_VLD f131_vld_2 (.in_1(in_2), .out_2(f131_vld_2_out_2));
  F131_CMPZ f131_cmpz_1 (.in_1(out_3), .ZF(ZF));
  not not_1 (not_1_out, f131_vld_1_out_2);
  not not_2 (not_2_out, f131_vld_2_out_2);
  or or_1 (BAF, not_1_out, not_2_out);
endmodule

// OR
module F131_OR (
  input  [7:0] in_1,
  input  [7:0] in_2,
  output [7:0] out_3,
  output ZF,
  output BAF
);

  wire f131_vld_1_out_2, f131_vld_2_out_2, not_1_out, not_2_out;

  assign out_3 = in_1 | in_2;  // OR_Gate or_1, 8 bits wide
  F131_VLD f131_vld_1 (.in_1(in_1), .out_2(f131_vld_1_out_2));
  F131_VLD f131_vld_2 (.in_1(in_2), .out_2(f131_vld_2_out_2));
  F131_CMPZ f131_cmpz_1 (.in_1(out_3), .ZF(ZF));
  not not_1 (not_1_out, f131_vld_1_out_2);
  not not_2 (not_2_out, f131_vld_2_out_2);
  or or_2 (BAF, not_1_out, not_2_out);
endmodule

// NOT
module F131_NOT (
  input  [7:0] in_1,
  output [7:0] out_2,
  output ZF,
  output BAF
);

  wire f131_vld_1_out_2;

  assign out_2 = ~in_1;  // NOT_Gate not_1, 8 bits wide
  F131_VLD f131_vld_1 (.in_1(in_1), .out_2(f131_vld_1_out_2));
  F131_CMPZ f131_cmpz_1 (.in_1(out_2), .ZF(ZF));
  not not_2 (BAF, f131_vld_1_out_2);
endmodule

// N1
module F131_N1 (
  input  [7:0] in_1,
  output [7:0] out_2,
  output ZF,
  output BAF
);

  wire f131_vld_1_out_2;
  wire [0:0] adder_1_out, adder_2_out, adder_3_out, adder_4_out;
  wire [1:0] adder_5_out, adder_6_out, or_1_out, or_2_out, or_3_out, or_4_out;
  wire [1:1] adder_1_cout, adder_2_cout, adder_3_cout, adder_4_cout;
  wire [2:0] adder_7_out, or_5_out, or_6_out;
  wire [2:2] adder_5_cout, adder_6_cout;
  wire [3:3] adder_7_cout;

  Adder #(.width(1)) adder_1 (.a(in_1[0]), .b(in_1[1]), .out(adder_1_out[0]), .cout(adder_1_cout[1]));  // open: cin
  Adder #(.width(1)) adder_2 (.a(in_1[2]), .b(in_1[3]), .out(adder_2_out[0]), .cout(adder_2_cout[1]));  // open: cin
  Adder #(.width(1)) adder_3 (.a(in_1[4]), .b(in_1[5]), .out(adder_3_out[0]), .cout(adder_3_cout[1]));  // open: cin
  Adder #(.width(1)) adder_4 (.a(in_1[6]), .b(in_1[7]), .out(adder_4_out[0]), .cout(adder_4_cout[1]));  // open: cin
  assign or_1_out = {1'b0, adder_1_out[0]} | {adder_1_cout[1], 1'b0};  // OR_Gate or_1, 2 bits wide
  Adder #(.width(2)) adder_5 (.a(or_1_out), .b(or_2_out), .out(adder_5_out), .cout(adder_5_cout[2]));  // open: cin
  assign or_2_out = {1'b0, adder_2_out[0]} | {adder_2_cout[1], 1'b0};  // OR_Gate or_2, 2 bits wide
  assign or_3_out = {1'b0, adder_3_out[0]} | {adder_3_cout[1], 1'b0};  // OR_Gate or_3, 2 bits wide
  Adder #(.width(2)) adder_6 (.a(or_3_out), .b(or_4_out), .out(adder_6_out), .cout(adder_6_cout[2]));  // open: cin
  assign or_4_out = {1'b0, adder_4_out[0]} | {adder_4_cout[1], 1'b0};  // OR_Gate or_4, 2 bits wide
  assign or_5_out = {1'b0, adder_5_out} | {adder_5_cout[2], 2'b00};  // OR_Gate or_5, 3 bits wide
  assign or_6_out = {1'b0, adder_6_out} | {adder_6_cout[2], 2'b00};  // OR_Gate or_6, 3 bits wide
  Adder #(.width(3)) adder_7 (.a(or_5_out), .b(or_6_out), .out(adder_7_out), .cout(adder_7_cout[3]));  // open: cin
  not not_1 (BAF, f131_vld_1_out_2);
  F131_VLD f131_vld_1 (.in_1(in_1), .out_2(f131_vld_1_out_2));
  assign out_2 = {{5{1'b0}}, adder_7_out} | {4'b0000, adder_7_cout[3], 3'b000};  // OR_Gate or_7, 8 bits wide
  F131_CMPZ f131_cmpz_1 (.in_1(out_2), .ZF(ZF));
endmodule

// N0
module F131_N0 (
  input  [7:0] in_1,
  output [7:0] out_2,
  output ZF
);

  wire [7:0] f131_not_1_out_2;

  F131_N1 f131_n1_1 (.in_1(f131_not_1_out_2), .out_2(out_2), .ZF(ZF));  // open: BAF
  F131_NOT f131_not_1 (.in_1(in_1), .out_2(f131_not_1_out_2));  // open: ZF, BAF
endmodule

// OP1
module F131_OP1 (
  input  [7:0] in_1,
  input  [7:0] in_2,
  output Z,
  output ZF,
  output BAF
);

  wire comparator_1_eq, comparator_1_gt, f131_vld_1_out_2, f131_vld_2_out_2, not_1_out, not_2_out;

  Comparator comparator_1 (.a(in_1), .b(in_2), .gt(comparator_1_gt), .eq(comparator_1_eq));  // open: lt
  not not_1 (not_1_out, f131_vld_1_out_2);
  F131_VLD f131_vld_1 (.in_1(in_1), .out_2(f131_vld_1_out_2));
  not not_2 (not_2_out, f131_vld_2_out_2);
  F131_VLD f131_vld_2 (.in_1(in_2), .out_2(f131_vld_2_out_2));
  or or_1 (Z, comparator_1_gt, comparator_1_eq);
  or or_2 (BAF, not_1_out, not_2_out);

  assign ZF = 1'b0;

  // Notes on the sheet:
  //   Z <- (X >= Y) 
endmodule

// OP2
module F131_OP2 (
  input  [7:0] in_1,
  input  [7:0] in_2,
  output Z,
  output ZF,
  output BAF
);

  wire f131_vld_1_out_2, f131_vld_2_out_2, not_1_out, not_2_out;
  wire [7:0] f131_neg_1_out_2;

  F131_NEG f131_neg_1 (.in_1(in_2), .out_2(f131_neg_1_out_2));  // open: ZF, BAF
  Comparator comparator_1 (.a(in_1), .b(f131_neg_1_out_2), .eq(Z));  // open: gt, lt
  not not_1 (not_1_out, f131_vld_1_out_2);
  F131_VLD f131_vld_1 (.in_1(in_1), .out_2(f131_vld_1_out_2));
  not not_2 (not_2_out, f131_vld_2_out_2);
  F131_VLD f131_vld_2 (.in_1(in_1), .out_2(f131_vld_2_out_2));
  F131_CMPZ f131_cmpz_1 (.in_1(in_1), .ZF(ZF));
  or or_1 (BAF, not_1_out, not_2_out);

  // Notes on the sheet:
  //   X == NEG Y
endmodule
