// Logisim project F193-mini.circ as structural Verilog: 24 circuits, main circuit F193ADD
module F193ADD (
  input  [7:0] X,
  input  [7:0] Y,
  output [7:0] Z,
  output ZF,
  output BAF
);

  wire comparator_1_lt, comparator_2_lt, not_1_out, not_2_out;
  wire [7:0] adder_1_out;
  wire [8:8] adder_1_cout, divider_1_rem;

  Adder adder_1 (.a(X), .b(Y), .out(adder_1_out), .cin(1'b0), .cout(adder_1_cout[8]));
  Comparator #(.mode("unsigned")) comparator_1 (.a(X), .b(8'hc1), .lt(comparator_1_lt));  // open: gt, eq
  Comparator #(.mode("unsigned")) comparator_2 (.a(Y), .b(8'hc1), .lt(comparator_2_lt));  // open: gt, eq
  Divider #(.width(9)) divider_1 (
    .a({adder_1_cout[8], adder_1_out}), .b(9'hc1), .upper({9{1'b0}}), .rem({divider_1_rem[8], Z}));  // open: out
  not not_1 (not_1_out, comparator_1_lt);
  not not_2 (not_2_out, comparator_2_lt);
  or or_1 (BAF, not_1_out, not_2_out);
  F193CMPZ f193cmpz_1 (.X(Z), .ZF(ZF));
endmodule

module F193NEG (
  input  [7:0] X,
  output [7:0] Z,
  output ZF,
  output BAF
);

  wire comparator_1_eq, comparator_1_gt, comparator_2_eq, comparator_2_gt;
  wire [7:0] subtractor_1_out;

  Subtractor subtractor_1 (.a(8'hc1), .b(X), .out(subtractor_1_out));  // open: bin, bout
  Comparator #(.mode("unsigned")) comparator_1 (
    .a(X), .b(8'hc1), .gt(comparator_1_gt), .eq(comparator_1_eq));  // open: lt
  assign Z = comparator_2_gt ? subtractor_1_out : 8'bz;  // Controlled_Buffer controlled_buffer_1
  Comparator #(.mode("unsigned")) comparator_2 (
    .a(X), .b({8{1'b0}}), .gt(comparator_2_gt), .eq(comparator_2_eq));  // open: lt
  or or_1 (BAF, comparator_1_gt, comparator_1_eq);
  assign Z = comparator_2_eq ? X : 8'bz;  // Controlled_Buffer controlled_buffer_2
  F193CMPZ f193cmpz_1 (.X(Z), .ZF(ZF));
endmodule

module F193SUB (
  input  [7:0] X,
  input  [7:0] Y,
  output [7:0] Z,
  output ZF,
  output BAF
);

  wire f193add_1_baf, f193neg_1_baf;
  wire [7:0] f193neg_1_z;

  F193NEG f193neg_1 (.X(Y), .Z(f193neg_1_z), .BAF(f193neg_1_baf));  // open: ZF
  F193ADD f193add_1 (.X(X), .Y(f193neg_1_z), .Z(Z), .BAF(f193add_1_baf));  // open: ZF
  or or_1 (BAF, f193add_1_baf, f193neg_1_baf);
  F193CMPZ f193cmpz_1 (.X(Z), .ZF(ZF));
endmodule

module F193MUL (
  input  [7:0] x,
  input  [7:0] y,
  output [7:0] Z,
  output ZF,
  output BAF
);

  wire comparator_1_eq, comparator_2_eq;
  wire [7:0] C1, multiplier_1_out;

  Multiplier multiplier_1 (.a(x), .b(y), .out(multiplier_1_out), .cin({8{1'b0}}), .cout(C1));
  Comparator #(.mode("unsigned")) comparator_1 (.a(x), .b(8'hc1), .eq(comparator_1_eq));  // open: gt, lt
  Comparator #(.mode("unsigned")) comparator_2 (.a(y), .b(8'hc1), .eq(comparator_2_eq));  // open: gt, lt
  Divider divider_1 (.a(multiplier_1_out), .b(8'hc1), .upper(C1), .rem(Z));  // open: out
  or or_1 (BAF, comparator_1_eq, comparator_2_eq);
  F193CMPZ f193cmpz_1 (.X(Z), .ZF(ZF));
endmodule

module F193DIV (
  input  [7:0] X,
  input  [7:0] Y,
  output [7:0] Z,
  output BAF,
  output ZF
);

  wire f193inv_1_baf, f193mul_1_baf;
  wire [7:0] f193inv_1_z;

  F193INV f193inv_1 (.X(Y), .Z(f193inv_1_z), .BAF(f193inv_1_baf));  // open: ZF
  F193MUL f193mul_1 (.x(X), .y(f193inv_1_z), .Z(Z), .BAF(f193mul_1_baf), .ZF(ZF));
  or or_1 (BAF, f193mul_1_baf, f193inv_1_baf);
endmodule

module F193_ALU (
  input  [7:0] OpCode,
  input  [7:0] X,
  input  [7:0] Y,
  output [7:0] DEBUG,
  output [7:0] Z,
  output BAF,
  output ZF,
  output BOF
);

  wire comparator_1_gt, not_1_out;
  wire [0:0] f193cmpz_1_zf, f193op1_1_z, f193op2_1_z, f193vld_1_z;
  wire [7:0] f193add_1_z, f193and_1_z, f193dec_1_z, f193div_1_z, f193inc_1_z, f193inv_1_z, f193mul_1_z,
       f193n0_1_z, f193n1_1_z, f193neg_1_z, f193not_1_z, f193op3_1_z, f193or_1_z, f193rol_1_z, f193ror_1_z,
       f193shl_1_z, f193shr_1_z, f193sub_1_z, f193xor_1_z;
  wire [9:8] f193add_1_baf, f193dec_1_zf, f193div_1_baf, f193inc_1_baf, f193inv_1_baf, f193mul_1_baf,
       f193neg_1_baf, f193sub_1_baf;
  wire [9:9] f193and_1_zf, f193n0_1_zf, f193n1_1_zf, f193not_1_zf, f193op3_1_baf, f193or_1_zf, f193rol_1_zf,
       f193ror_1_zf, f193shl_1_zf, f193shr_1_zf, f193xor_1_zf;
  wire [10:0] multiplexer_1_out, multiplexer_2_out;

  F193ADD f193add_1 (.X(X), .Y(Y), .Z(f193add_1_z), .BAF(f193add_1_baf[8]), .ZF(f193add_1_baf[9]));
  F193SUB f193sub_1 (.X(X), .Y(Y), .Z(f193sub_1_z), .BAF(f193sub_1_baf[8]), .ZF(f193sub_1_baf[9]));
  F193DIV f193div_1 (.X(X), .Y(Y), .Z(f193div_1_z), .BAF(f193div_1_baf[8]), .ZF(f193div_1_baf[9]));
  F193XOR f193xor_1 (.X(X), .Y(Y), .Z(f193xor_1_z), .ZF(f193xor_1_zf[9]));
  F193AND f193and_1 (.X(X), .Y(Y), .Z(f193and_1_z), .ZF(f193and_1_zf[9]));
  F193OR f193or_1 (.X(X), .Y(Y), .Z(f193or_1_z), .ZF(f193or_1_zf[9]));
  F193NEG f193neg_1 (.X(X), .Z(f193neg_1_z), .BAF(f193neg_1_baf[8]), .ZF(f193neg_1_baf[9]));
  F193INC f193inc_1 (.X(X), .Z(f193inc_1_z), .ZF(f193inc_1_baf[9]), .BAF(f193inc_1_baf[8]));
  F193DEC f193dec_1 (.X(X), .Z(f193dec_1_z), .BAF(f193dec_1_zf[9]), .ZF(f193dec_1_zf[8]));
  F193INV f193inv_1 (.X(X), .Z(f193inv_1_z), .BAF(f193inv_1_baf[8]), .ZF(f193inv_1_baf[9]));
  F193SHL f193shl_1 (.X(X), .Z(f193shl_1_z), .ZF(f193shl_1_zf[9]));
  F193SHR f193shr_1 (.X(X), .Z(f193shr_1_z), .ZF(f193shr_1_zf[9]));
  F193ROL f193rol_1 (.X(X), .Z(f193rol_1_z), .ZF(f193rol_1_zf[9]));
  F193ROR f193ror_1 (.X(X), .Z(f193ror_1_z), .ZF(f193ror_1_zf[9]));
  F193NOT f193not_1 (.X(X), .Z(f193not_1_z), .ZF(f193not_1_zf[9]));
  F193N1 f193n1_1 (.X(X), .Z(f193n1_1_z), .ZF(f193n1_1_zf[9]));
  F193N0 f193n0_1 (.X(X), .Z(f193n0_1_z), .ZF(f193n0_1_zf[9]));
  F193OP3 f193op3_1 (.X(X), .Z(f193op3_1_z), .BAF(f193op3_1_baf[9]));
  F193VLD f193vld_1 (.X(X), .Z(f193vld_1_z[0]));
  F193CMPZ f193cmpz_1 (.X(X), .ZF(f193cmpz_1_zf[0]));
  F193OP1 f193op1_1 (.X(X), .Y(Y), .Z(f193op1_1_z[0]));
  F193OP2 f193op2_1 (.X(X), .Y(Y), .Z(f193op2_1_z[0]));
  F193MUL f193mul_1 (.x(X), .y(Y), .Z(f193mul_1_z), .BAF(f193mul_1_baf[8]), .ZF(f193mul_1_baf[9]));
  ROM rom_1 (.addr(OpCode), .data(DEBUG));  // open: sel
  assign {BOF, ZF, BAF, Z} = not_1_out ? multiplexer_1_out : 11'bz;  // Controlled_Buffer controlled_buffer_1
  Multiplexer #(.select(4), .width(11)) multiplexer_1 (
    .in0(11'h400), .in1({1'b0, f193add_1_baf, f193add_1_z}), .in2({1'b0, f193sub_1_baf, f193sub_1_z}),
    .in3({1'b0, f193mul_1_baf, f193mul_1_z}), .in4({1'b0, f193div_1_baf, f193div_1_z}),
    .in5({1'b0, f193xor_1_zf[9], 1'b0, f193xor_1_z}), .in6({1'b0, f193and_1_zf[9], 1'b0, f193and_1_z}),
    .in7({1'b0, f193or_1_zf[9], 1'b0, f193or_1_z}), .in8({1'b0, f193neg_1_baf, f193neg_1_z}),
    .in9({1'b0, f193inc_1_baf, f193inc_1_z}), .in10({1'b0, f193dec_1_zf, f193dec_1_z}),
    .in11({1'b0, f193inv_1_baf, f193inv_1_z}), .in12({1'b0, f193shl_1_zf[9], 1'b0, f193shl_1_z}),
    .in13({1'b0, f193shr_1_zf[9], 1'b0, f193shr_1_z}), .in14({1'b0, f193rol_1_zf[9], 1'b0, f193rol_1_z}),
    .in15({1'b0, f193ror_1_zf[9], 1'b0, f193ror_1_z}), .out(multiplexer_1_out), .sel(DEBUG[3:0]), .en(1'b1));
  Multiplexer #(.select(4), .width(11)) multiplexer_2 (
    .in1({1'b0, f193not_1_zf[9], 1'b0, f193not_1_z}), .in2({1'b0, f193n1_1_zf[9], 1'b0, f193n1_1_z}),
    .in3({1'b0, f193n0_1_zf[9], 1'b0, f193n0_1_z}), .in4({1'b0, f193op3_1_baf[9], 1'b0, f193op3_1_z}),
    .in5({{10{1'b0}}, f193vld_1_z[0]}), .in6({{10{1'b0}}, f193cmpz_1_zf[0]}),
    .in7({{10{1'b0}}, f193op1_1_z[0]}), .in8({{10{1'b0}}, f193op2_1_z[0]}), .out(multiplexer_2_out),
    .sel(DEBUG[7:4]), .en(1'b1));  // open: in0, in9, in10, in11, in12, in13, in14, in15
  not not_1 (not_1_out, comparator_1_gt);
  assign {BOF, ZF, BAF, Z} = comparator_1_gt ? multiplexer_2_out : 11'bz;  // Controlled_Buffer controlled_buffer_2
  Comparator #(.width(4), .mode("unsigned")) comparator_1 (
    .a(DEBUG[7:4]), .b(4'b0000), .gt(comparator_1_gt));  // open: eq, lt

  // Other names for the same wires on the sheet: OPC_IN_1[3:0] = DEBUG[3:0]; OPC_IN_2[3:0] = DEBUG[7:4]

  // Notes on the sheet:
  //   contents of rom_1 (hex, n*v repeats v):
  //   0 50 8 9 a 60 b 0 c d e f 10 20 30 0 1 2 3 4 8*0 5 6 7 57*0 70 80 40
endmodule

module F193INV (
  input  [7:0] X,
  output [7:0] Z,
  output ZF,
  output BAF
);

  wire comparator_1_eq, comparator_1_gt;

  Comparator #(.mode("unsigned")) comparator_1 (
    .a(X), .b(8'hc1), .gt(comparator_1_gt), .eq(comparator_1_eq));  // open: lt
  ROM rom_1 (.addr(X), .data(Z));  // open: sel
  or or_1 (BAF, comparator_1_gt, comparator_1_eq);
  F193CMPZ f193cmpz_1 (.X(Z), .ZF(ZF));

  // Notes on the sheet:
  //   contents of rom_1 (hex, n*v repeats v):
  //   0 1 61 81 91 74 a1 8a a9 2b 3a 9e b1 68 45 67 b5 9f 76 3d 1d 2e 4f 2a b9 8b 34 8f 83 14 94 89 bb 75
  //   b0 b6 3b 78 7f 63 6f 71 17 9 88 a3 15 73 bd 82 a6 35 1a 33 a8 ba a2 95 a 24 4a 13 a5 90 be 62 9b 79
  //   58 e 5b 57 7e 9c 3c af a0 bc 92 16 98 70 99 64 6c 6d 65 47 44 b4 b2 46 6b 6e 9a 80 bf 2 41 27 53 56
  //   7b f d 7d 7a 5c 54 55 5d 28 51 29 ab 2f 5 21 12 85 25 43 6a 66 b3 69 48 26 5f 3 31 1c ae 77 9d b7 2c
  //   1f 7 19 8e a7 8c 1b 3f 4 4e ac 1e 39 b8 aa 50 52 5e 42 49 86 b 11 4c 6 38 2d ad 3e 32 8d 36 8 97 72
  //   93 a4 84 4b 22 c 5a 7c 59 10 23 87 96 18 37 20 4d 30 40 60 c0
endmodule

module F193VLD (
  input  [7:0] X,
  output Z
);

  Comparator #(.mode("unsigned")) comparator_1 (.a(X), .b(8'hc1), .lt(Z));  // open: gt, eq
endmodule

module F193INC (
  input  [7:0] X,
  output [7:0] Z,
  output ZF,
  output BAF
);

  F193ADD f193add_1 (.X(X), .Y(8'h1), .Z(Z), .BAF(BAF), .ZF(ZF));
endmodule

module F193DEC (
  input  [7:0] X,
  output [7:0] Z,
  output BAF,
  output ZF
);

  F193SUB f193sub_1 (.X(X), .Y(8'h1), .Z(Z), .BAF(BAF), .ZF(ZF));
endmodule

module F193CMPZ (
  input  [7:0] X,
  output ZF
);

  Comparator #(.mode("unsigned")) comparator_1 (.a(X), .b({8{1'b0}}), .eq(ZF));  // open: gt, lt
endmodule

module F193SHL (
  input  [7:0] X,
  output [7:0] Z,
  output ZF
);

  Shifter shifter_1 (.in(X), .\dist (3'b001), .out(Z));
  F193CMPZ f193cmpz_1 (.X(Z), .ZF(ZF));
endmodule

module F193SHR (
  input  [7:0] X,
  output [7:0] Z,
  output ZF
);

  Shifter #(.shift("lr")) shifter_1 (.in(X), .\dist (3'b001), .out(Z));
  F193CMPZ f193cmpz_1 (.X(Z), .ZF(ZF));
endmodule

module F193ROL (
  input  [7:0] X,
  output [7:0] Z,
  output ZF
);

  Shifter #(.shift("rl")) shifter_1 (.in(X), .\dist (3'b001), .out(Z));
  F193CMPZ f193cmpz_1 (.X(Z), .ZF(ZF));
endmodule

module F193ROR (
  input  [7:0] X,
  output [7:0] Z,
  output ZF
);

  Shifter #(.shift("rr")) shifter_1 (.in(X), .\dist (3'b001), .out(Z));
  F193CMPZ f193cmpz_1 (.X(Z), .ZF(ZF));
endmodule

module F193XOR (
  input  [7:0] X,
  input  [7:0] Y,
  output [7:0] Z,
  output ZF
);

  xor xor_1 (Z[7], X[7], Y[7]);
  xor xor_2 (Z[0], X[0], Y[0]);
  xor xor_3 (Z[1], X[1], Y[1]);
  xor xor_4 (Z[2], X[2], Y[2]);
  xor xor_5 (Z[3], X[3], Y[3]);
  xor xor_6 (Z[4], X[4], Y[4]);
  xor xor_7 (Z[5], X[5], Y[5]);
  xor xor_8 (Z[6], X[6], Y[6]);
  F193CMPZ f193cmpz_1 (.X(Z), .ZF(ZF));
endmodule

module F193AND (
  input  [7:0] X,
  input  [7:0] Y,
  output [7:0] Z,
  output ZF
);

  and and_1 (Z[7], X[7], Y[7]);
  and and_2 (Z[0], X[0], Y[0]);
  and and_3 (Z[1], X[1], Y[1]);
  and and_4 (Z[2], X[2], Y[2]);
  and and_5 (Z[3], X[3], Y[3]);
  and and_6 (Z[4], X[4], Y[4]);
  and and_7 (Z[5], X[5], Y[5]);
  and and_8 (Z[6], X[6], Y[6]);
  F193CMPZ f193cmpz_1 (.X(Z), .ZF(ZF));
endmodule

module F193OR (
  input  [7:0] X,
  input  [7:0] Y,
  output [7:0] Z,
  output ZF
);

  or or_1 (Z[7], X[7], Y[7]);
  or or_2 (Z[0], X[0], Y[0]);
  or or_3 (Z[1], X[1], Y[1]);
  or or_4 (Z[2], X[2], Y[2]);
  or or_5 (Z[3], X[3], Y[3]);
  or or_6 (Z[4], X[4], Y[4]);
  or or_7 (Z[5], X[5], Y[5]);
  or or_8 (Z[6], X[6], Y[6]);
  F193CMPZ f193cmpz_1 (.X(Z), .ZF(ZF));
endmodule

module F193NOT (
  input  [7:0] X,
  output [7:0] Z,
  output ZF
);

  not not_1 (Z[0], X[0]);
  not not_2 (Z[1], X[1]);
  not not_3 (Z[2], X[2]);
  not not_4 (Z[3], X[3]);
  not not_5 (Z[4], X[4]);
  not not_6 (Z[5], X[5]);
  not not_7 (Z[6], X[6]);
  not not_8 (Z[7], X[7]);
  F193CMPZ f193cmpz_1 (.X(Z), .ZF(ZF));
endmodule

module F193N1 (
  input  [7:0] X,
  output [7:0] Z,
  output ZF
);

  wire not_1_out, not_2_out, not_3_out, not_4_out, not_5_out, not_6_out, not_7_out, not_8_out;
  wire [7:0] adder_1_out, adder_2_out, adder_3_out, adder_5_out, adder_6_out, controlled_buffer_1_out,
       controlled_buffer_3_out, controlled_buffer_5_out, controlled_buffer_7_out, controlled_buffer_8_out,
       controlled_buffer_9_out, controlled_buffer_11_out, controlled_buffer_13_out, controlled_buffer_14_out,
       controlled_buffer_15_out;

  assign controlled_buffer_1_out = X[0] ? {8{1'b0}} : 8'bz;  // Controlled_Buffer controlled_buffer_1
  not not_1 (not_1_out, X[0]);
  Adder adder_1 (.a(controlled_buffer_1_out), .b(8'h1), .out(adder_1_out));  // open: cin, cout
  assign adder_1_out = not_1_out ? {8{1'b0}} : 8'bz;  // Controlled_Buffer controlled_buffer_2
  assign controlled_buffer_3_out = X[1] ? adder_1_out : 8'bz;  // Controlled_Buffer controlled_buffer_3
  Adder adder_2 (.a(controlled_buffer_3_out), .b(8'h1), .out(adder_2_out));  // open: cin, cout
  assign adder_2_out = not_2_out ? adder_1_out : 8'bz;  // Controlled_Buffer controlled_buffer_4
  not not_2 (not_2_out, X[1]);
  assign controlled_buffer_5_out = X[2] ? adder_2_out : 8'bz;  // Controlled_Buffer controlled_buffer_5
  not not_3 (not_3_out, X[2]);
  Adder adder_3 (.a(controlled_buffer_5_out), .b(8'h1), .out(adder_3_out));  // open: cin, cout
  assign adder_3_out = not_3_out ? adder_2_out : 8'bz;  // Controlled_Buffer controlled_buffer_6
  assign controlled_buffer_7_out = X[3] ? adder_3_out : 8'bz;  // Controlled_Buffer controlled_buffer_7
  assign controlled_buffer_8_out = not_4_out ? adder_3_out : 8'bz;  // Controlled_Buffer controlled_buffer_8
  not not_4 (not_4_out, X[3]);
  assign controlled_buffer_9_out = X[4] ? controlled_buffer_8_out : 8'bz;  // Controlled_Buffer controlled_buffer_9
  Adder adder_4 (.a(controlled_buffer_7_out), .b(8'h1), .out(controlled_buffer_8_out));  // open: cin, cout
  Adder adder_5 (.a(controlled_buffer_9_out), .b(8'h1), .out(adder_5_out));  // open: cin, cout
  assign adder_5_out = not_5_out ? controlled_buffer_8_out : 8'bz;  // Controlled_Buffer controlled_buffer_10
  not not_5 (not_5_out, X[4]);
  assign controlled_buffer_11_out = X[5] ? adder_5_out : 8'bz;  // Controlled_Buffer controlled_buffer_11
  not not_6 (not_6_out, X[5]);
  Adder adder_6 (.a(controlled_buffer_11_out), .b(8'h1), .out(adder_6_out));  // open: cin, cout
  assign adder_6_out = not_6_out ? adder_5_out : 8'bz;  // Controlled_Buffer controlled_buffer_12
  assign controlled_buffer_13_out = X[6] ? adder_6_out : 8'bz;  // Controlled_Buffer controlled_buffer_13
  assign controlled_buffer_14_out = not_7_out ? adder_6_out : 8'bz;  // Controlled_Buffer controlled_buffer_14
  not not_7 (not_7_out, X[6]);
  Adder adder_7 (.a(controlled_buffer_13_out), .b(8'h1), .out(controlled_buffer_14_out));  // open: cin, cout
  assign controlled_buffer_15_out = X[7] ? controlled_buffer_14_out : 8'bz;  // Controlled_Buffer controlled_buffer_15
  Adder adder_8 (.a(controlled_buffer_15_out), .b(8'h1), .out(Z));  // open: cin, cout
  assign Z = not_8_out ? controlled_buffer_14_out : 8'bz;  // Controlled_Buffer controlled_buffer_16
  not not_8 (not_8_out, X[7]);
  F193CMPZ f193cmpz_1 (.X(Z), .ZF(ZF));
endmodule

module F193N0 (
  input  [7:0] X,
  output [7:0] Z,
  output ZF
);

  wire not_1_out, not_2_out, not_3_out, not_4_out, not_5_out, not_6_out, not_7_out, not_8_out;
  wire [7:0] adder_2_out, adder_3_out, adder_5_out, adder_6_out, adder_7_out, controlled_buffer_1_out,
       controlled_buffer_2_out, controlled_buffer_3_out, controlled_buffer_5_out, controlled_buffer_7_out,
       controlled_buffer_8_out, controlled_buffer_9_out, controlled_buffer_11_out, controlled_buffer_13_out,
       controlled_buffer_15_out, f193not_1_z;

  F193NOT f193not_1 (.X(X), .Z(f193not_1_z));  // open: ZF
  assign controlled_buffer_1_out = f193not_1_z[0] ? {8{1'b0}} : 8'bz;  // Controlled_Buffer controlled_buffer_1
  assign controlled_buffer_2_out = not_1_out ? {8{1'b0}} : 8'bz;  // Controlled_Buffer controlled_buffer_2
  not not_1 (not_1_out, f193not_1_z[0]);
  Adder adder_1 (.a(controlled_buffer_1_out), .b(8'h1), .out(controlled_buffer_2_out));  // open: cin, cout
  assign controlled_buffer_3_out = f193not_1_z[1] ? controlled_buffer_2_out : 8'bz;  // Controlled_Buffer controlled_buffer_3
  Adder adder_2 (.a(controlled_buffer_3_out), .b(8'h1), .out(adder_2_out));  // open: cin, cout
  assign adder_2_out = not_2_out ? controlled_buffer_2_out : 8'bz;  // Controlled_Buffer controlled_buffer_4
  not not_2 (not_2_out, f193not_1_z[1]);
  assign controlled_buffer_5_out = f193not_1_z[2] ? adder_2_out : 8'bz;  // Controlled_Buffer controlled_buffer_5
  not not_3 (not_3_out, f193not_1_z[2]);
  Adder adder_3 (.a(controlled_buffer_5_out), .b(8'h1), .out(adder_3_out));  // open: cin, cout
  assign adder_3_out = not_3_out ? adder_2_out : 8'bz;  // Controlled_Buffer controlled_buffer_6
  assign controlled_buffer_7_out = f193not_1_z[3] ? adder_3_out : 8'bz;  // Controlled_Buffer controlled_buffer_7
  assign controlled_buffer_8_out = not_4_out ? adder_3_out : 8'bz;  // Controlled_Buffer controlled_buffer_8
  not not_4 (not_4_out, f193not_1_z[3]);
  assign controlled_buffer_9_out = f193not_1_z[4] ? controlled_buffer_8_out : 8'bz;  // Controlled_Buffer controlled_buffer_9
  Adder adder_4 (.a(controlled_buffer_7_out), .b(8'h1), .out(controlled_buffer_8_out));  // open: cin, cout
  Adder adder_5 (.a(controlled_buffer_9_out), .b(8'h1), .out(adder_5_out));  // open: cin, cout
  assign adder_5_out = not_5_out ? controlled_buffer_8_out : 8'bz;  // Controlled_Buffer controlled_buffer_10
  not not_5 (not_5_out, f193not_1_z[4]);
  assign controlled_buffer_11_out = f193not_1_z[5] ? adder_5_out : 8'bz;  // Controlled_Buffer controlled_buffer_11
  not not_6 (not_6_out, f193not_1_z[5]);
  Adder adder_6 (.a(controlled_buffer_11_out), .b(8'h1), .out(adder_6_out));  // open: cin, cout
  assign adder_6_out = not_6_out ? adder_5_out : 8'bz;  // Controlled_Buffer controlled_buffer_12
  assign controlled_buffer_13_out = f193not_1_z[6] ? adder_6_out : 8'bz;  // Controlled_Buffer controlled_buffer_13
  Adder adder_7 (.a(controlled_buffer_13_out), .b(8'h1), .out(adder_7_out));  // open: cin, cout
  assign adder_7_out = not_7_out ? adder_6_out : 8'bz;  // Controlled_Buffer controlled_buffer_14
  not not_7 (not_7_out, f193not_1_z[6]);
  assign controlled_buffer_15_out = f193not_1_z[7] ? adder_7_out : 8'bz;  // Controlled_Buffer controlled_buffer_15
  not not_8 (not_8_out, f193not_1_z[7]);
  Adder adder_8 (.a(controlled_buffer_15_out), .b(8'h1), .out(Z));  // open: cin, cout
  assign Z = not_8_out ? adder_7_out : 8'bz;  // Controlled_Buffer controlled_buffer_16
  F193CMPZ f193cmpz_1 (.X(Z), .ZF(ZF));
endmodule

module F193OP1 (
  input  [7:0] X,
  input  [7:0] Y,
  output Z
);

  wire comparator_1_eq, comparator_1_lt;

  Comparator #(.mode("unsigned")) comparator_1 (.a(X), .b(Y), .eq(comparator_1_eq), .lt(comparator_1_lt));  // open: gt
  or or_1 (Z, comparator_1_eq, comparator_1_lt);
endmodule

module F193OP2 (
  input  [7:0] X,
  input  [7:0] Y,
  output Z
);

  wire [7:0] f193neg_1_z;

  Comparator #(.mode("unsigned")) comparator_1 (.a(X), .b(f193neg_1_z), .eq(Z));  // open: gt, lt
  F193NEG f193neg_1 (.X(Y), .Z(f193neg_1_z));  // open: BAF, ZF
endmodule

module F193OP3 (
  input  [7:0] X,
  output [7:0] Z,
  output BAF
);

  wire comparator_1_eq, comparator_1_gt;

  Comparator #(.mode("unsigned")) comparator_1 (
    .a(X), .b(8'hc1), .gt(comparator_1_gt), .eq(comparator_1_eq));  // open: lt
  ROM rom_1 (.addr(X), .data(Z));  // open: sel
  or or_1 (BAF, comparator_1_gt, comparator_1_eq);

  // Notes on the sheet:
  //   contents of rom_1 (hex, n*v repeats v):
  //   0 1 30*0 2
endmodule
