// Logisim project Z9-MINI.circ as structural Verilog: 9 circuits, main circuit main
module main (
  input  [3:0] OpCode,
  input  [3:0] X,
  input  [3:0] Y,
  output [3:0] Z,
  output BAF
);

  ALU alu_1 (.OpCode(OpCode), .X(X), .Y(Y), .Z(Z), .BAF(BAF));

  // Notes on the sheet:
  //   ADD -> 0000
  //   MUL -> 0001
  //   INV -> 0010
  //   AND -> 0011
  //   OR -> 0100
  //   NOT -> 0101
  //   SQRT -> 0110
  //   Simple ALU for Z_9 ring
endmodule

module Z9_ADD (
  input  [3:0] X,
  input  [3:0] Y,
  output [3:0] Z,
  output BAF
);

  wire comparator_1_lt, comparator_2_lt, not_1_out, not_2_out;
  wire [0:0] adder_1_cout;
  wire [3:0] adder_1_out;

  Comparator #(.width(4), .mode("unsigned")) comparator_1 (.a(X), .b(4'b1001), .lt(comparator_1_lt));  // open: gt, eq
  Comparator #(.width(4), .mode("unsigned")) comparator_2 (.a(Y), .b(4'b1001), .lt(comparator_2_lt));  // open: gt, eq
  Adder #(.width(4)) adder_1 (.a(X), .b(Y), .out(adder_1_out), .cin(1'b0), .cout(adder_1_cout[0]));
  not not_1 (not_1_out, comparator_1_lt);
  not not_2 (not_2_out, comparator_2_lt);
  Divider #(.width(4)) divider_1 (
    .a(adder_1_out), .b(4'b1001), .upper({3'b000, adder_1_cout[0]}), .rem(Z));  // open: out
  or or_1 (BAF, not_1_out, not_2_out);

  // Notes on the sheet:
  //   pasiziuret kas cia per spliteris ir kodel is ino eina
endmodule

module Z9_MUL (
  input  [3:0] X,
  input  [3:0] Y,
  output [3:0] Z,
  output BAF
);

  wire comparator_1_lt, comparator_2_lt, not_1_out, not_2_out;
  wire [3:0] multiplier_1_cout, multiplier_1_out;

  Comparator #(.width(4), .mode("unsigned")) comparator_1 (.a(X), .b(4'b1001), .lt(comparator_1_lt));  // open: gt, eq
  Comparator #(.width(4), .mode("unsigned")) comparator_2 (.a(Y), .b(4'b1001), .lt(comparator_2_lt));  // open: gt, eq
  Multiplier #(.width(4)) multiplier_1 (.a(X), .b(Y), .out(multiplier_1_out), .cin(4'b0000), .cout(multiplier_1_cout));
  not not_1 (not_1_out, comparator_1_lt);
  not not_2 (not_2_out, comparator_2_lt);
  Divider #(.width(4)) divider_1 (.a(multiplier_1_out), .b(4'b1001), .upper(multiplier_1_cout), .rem(Z));  // open: out
  or or_1 (BAF, not_1_out, not_2_out);

  // Notes on the sheet:
  //   nebutina spliterio cia, specialiai balamutina
endmodule

module Z9_INV (
  input  [3:0] X,
  output [3:0] Z,
  output BAF
);

  ROM #(.addrWidth(4), .dataWidth(4)) rom_1 (.addr(X), .data(Z), .sel(1'b1));
  Comparator #(.width(4)) comparator_1 (.a(Z), .b(4'b0000), .eq(BAF));  // open: gt, lt

  // Notes on the sheet:
  //   selection turi but vienas
  //   cia read only memory
  //   contents of rom_1 (hex, n*v repeats v):
  //   0 1 5 0 7 2 0 4 8
  //   if Z == 0 then BAF <- 1
endmodule

module Z9_AND (
  input  [3:0] X,
  input  [3:0] Y,
  output [3:0] Z,
  output BAF
);

  assign Z = X & Y;  // AND_Gate and_1, 4 bits wide

  assign BAF = 1'b0;
endmodule

module Z9_OR (
  input  [3:0] X,
  input  [3:0] Y,
  output [3:0] Z,
  output BAF
);

  assign Z = X | Y;  // OR_Gate or_1, 4 bits wide

  assign BAF = 1'b0;
endmodule

module Z9_NOT (
  input  [3:0] X,
  output [3:0] Z,
  output BAF
);

  assign Z = ~X;  // NOT_Gate not_1, 4 bits wide

  assign BAF = 1'b0;
endmodule

module Z9_SQRT (
  input  [3:0] in_1,
  output [3:0] Z,
  output BAF
);

  wire and_4_out, and_5_out, and_6_out, not_1_out, not_2_out, not_3_out, not_4_out, not_5_out, not_6_out,
       not_7_out, not_8_out, not_9_out, not_10_out;

  not not_1 (not_1_out, in_1[3]);
  not not_2 (not_2_out, in_1[3]);
  not not_3 (not_3_out, in_1[1]);
  not not_4 (not_4_out, in_1[0]);
  not not_5 (not_5_out, in_1[3]);
  not not_6 (not_6_out, in_1[2]);
  not not_7 (not_7_out, in_1[1]);
  not not_8 (not_8_out, in_1[2]);
  not not_9 (not_9_out, in_1[0]);
  not not_10 (not_10_out, in_1[1]);
  and and_1 (Z[2], not_1_out, in_1[2], in_1[1], in_1[0]);
  and and_2 (Z[1], not_2_out, in_1[2], not_3_out, not_4_out);
  and and_3 (Z[0], not_5_out, not_6_out, not_7_out, in_1[0]);
  and and_4 (and_4_out, not_8_out, in_1[1]);
  and and_5 (and_5_out, in_1[1], not_9_out);
  and and_6 (and_6_out, in_1[2], not_10_out, in_1[0]);
  or or_1 (BAF, and_4_out, and_5_out, and_6_out, in_1[3]);

  assign Z[3] = 1'b0;

  // Notes on the sheet:
  //   cia su truth table darom
endmodule

module ALU (
  input  [3:0] OpCode,
  input  [3:0] X,
  input  [3:0] Y,
  output [3:0] Z,
  output BAF
);

  wire BAF_ADD, BAF_AND, BAF_INV, BAF_MUL, BAF_NOT, BAF_OR, BAF_SQRT;
  wire [3:0] Z_ADD, Z_AND, Z_INV, Z_MUL, Z_NOT, Z_OR, Z_SQRT;

  Z9_ADD z9_add_1 (.X(X), .Y(Y), .Z(Z_ADD), .BAF(BAF_ADD));
  Z9_MUL z9_mul_1 (.X(X), .Y(Y), .Z(Z_MUL), .BAF(BAF_MUL));
  Z9_INV z9_inv_1 (.X(X), .Z(Z_INV), .BAF(BAF_INV));
  Z9_AND z9_and_1 (.X(X), .Y(Y), .Z(Z_AND), .BAF(BAF_AND));
  Z9_OR z9_or_1 (.X(X), .Y(Y), .Z(Z_OR), .BAF(BAF_OR));
  Z9_NOT z9_not_1 (.X(X), .Z(Z_NOT), .BAF(BAF_NOT));
  Z9_SQRT z9_sqrt_1 (.in_1(X), .Z(Z_SQRT), .BAF(BAF_SQRT));
  Multiplexer #(.select(4), .width(4)) multiplexer_1 (
    .in0(Z_ADD), .in1(Z_MUL), .in2(Z_INV), .in3(Z_AND), .in4(Z_OR), .in5(Z_NOT), .in6(Z_SQRT), .in7(4'b0000),
    .in8(4'b0000), .in9(4'b0000), .in10(4'b0000), .in11(4'b0000), .in12(4'b0000), .in13(4'b0000),
    .in14(4'b0000), .in15(4'b0000), .out(Z), .sel(OpCode));  // open: en
  Multiplexer #(.select(4)) multiplexer_2 (
    .in0(BAF_ADD), .in1(BAF_MUL), .in2(BAF_INV), .in3(BAF_AND), .in4(BAF_OR), .in5(BAF_NOT), .in6(BAF_SQRT),
    .in7(1'b0), .in8(1'b0), .in9(1'b0), .in10(1'b0), .in11(1'b0), .in12(1'b0), .in13(1'b0), .in14(1'b0),
    .in15(1'b0), .out(BAF), .sel(OpCode));  // open: en
endmodule
