// Logisim project CPU_Monika.circ as structural Verilog: 5 circuits, main circuit main
// ALU
module main (
  output [7:0] out_1,
  output [7:0] out_2,
  output [7:0] out_3,
  output [7:0] out_4,
  output [7:0] out_5,
  output [7:0] out_6,
  output [7:0] out_7,
  output [7:0] out_8,
  output [7:0] out_9,
  output [7:0] out_10,
  output [7:0] out_11,
  output [7:0] out_12,
  output [7:0] out_13,
  output [7:0] out_14,
  output [7:0] out_15,
  output [7:0] out_16,
  output [7:0] out_17,
  output [7:0] out_18,
  output [7:0] out_19,
  output [7:0] out_20,
  output [7:0] out_21
);

  wire BAF, clk, clock_1_out, comparator_1_lt, Dload, dwrite, HALT, Imload, IRCload, IRRload, keepZF_BAF,
       main_1_baf, main_1_zf, nHALT, or_1_out, PCload, PCsel, ReadWrite, SP_en, SP_sub, ZF;
  wire [1:0] adrsel, regsel;
  wire [3:0] dregsel, sregsel;
  wire [7:0] aluop, main_1_out_4, multiplexer_1_out, multiplexer_3_out, PC, pc_adder_1_out_2, ram_1_data,
       register_1_q, register_3_q, SP, sp_adder_subtractor_1_out_3;

  Multiplexer #(.width(8), .enable("false")) multiplexer_1 (
    .in0(out_2), .in1(PC), .out(multiplexer_1_out), .sel(Dload));
  SP_adder_subtractor sp_adder_subtractor_1 (.in_1(SP), .out_3(sp_adder_subtractor_1_out_3), .in_2(SP_sub));
  Multiplexer #(.select(2), .width(8), .enable("false")) multiplexer_2 (
    .in0(PC), .in1(out_3), .in2(out_5), .in3(SP), .out(out_1), .sel(adrsel));
  Register u_SP (.D(sp_adder_subtractor_1_out_3), .en(SP_en), .Q(SP), .clk(clk));  // open: clr
  RAM #(.bus("separate")) ram_1 (
    .addr(out_1), .din(multiplexer_1_out), .data(ram_1_data), .str(ReadWrite), .clk(clk));  // open: sel, ld, clr
  Register register_1 (.D(ram_1_data), .en(IRCload), .Q(register_1_q), .clk(clk));  // open: clr
  LED led_1 (.in(HALT));
  Register register_2 (.D(ram_1_data), .en(Imload), .Q(out_3), .clk(clk));  // open: clr
  Register register_3 (.D(ram_1_data), .en(IRRload), .Q(register_3_q), .clk(clk));  // open: clr
  Multiplexer #(.width(8), .enable("false")) multiplexer_3 (
    .in0(out_3), .in1(pc_adder_1_out_2), .out(multiplexer_3_out), .sel(PCsel));
  Decoder_Logic decoder_logic_1 (
    .in_3(register_1_q), .in_4(register_3_q), .dregsel(dregsel), .sregsel(sregsel), .out_7(aluop),
    .out_8(IRCload), .out_9(IRRload), .out_10(Imload), .out_11(ReadWrite), .ZF(ZF), .BAF(BAF),
    .out_12(PCload), .out_13(PCsel), .out_15(adrsel), .out_14(dwrite), .out_16(Dload), .out_17(regsel),
    .out_18(SP_en), .out_19(SP_sub), .out_20(keepZF_BAF), .out_21(nHALT));
  Register u_PC (.D(multiplexer_3_out), .en(PCload), .Q(PC), .clk(clk));  // open: clr
  PC_Adder pc_adder_1 (.in_1(PC), .out_2(pc_adder_1_out_2));
  Multiplexer #(.select(2), .width(8), .enable("false")) multiplexer_4 (
    .in0(out_3), .in1(out_5), .in2(ram_1_data), .in3(main_1_out_4), .out(out_4), .sel(regsel));
  Register_File register_file_1 (
    .dwrite(dwrite), .dregsel(dregsel), .in_3(out_4), .sregsel(sregsel), .R0(out_6), .R1(out_7),
    .dbus(out_2), .R2(out_8), .R3(out_9), .R4(out_10), .R5(out_11), .R6(out_12), .R7(out_13), .R8(out_14),
    .R9(out_15), .R10(out_16), .R11(out_17), .R12(out_18), .R13(out_19), .sbus(out_5), .R14(out_20),
    .R15(out_21));
  ALU_10_var_Final_pataisyta_main main_1 (
    .in_1(out_2), .in_2(out_5), .in_3(aluop), .out_4(main_1_out_4), .ZF(main_1_zf), .BAF(main_1_baf));  // open: BOF
  Clock clock_1 (.out(clock_1_out));
  Comparator #(.mode("unsigned")) comparator_1 (.a(PC), .b(8'h1), .lt(comparator_1_lt));  // open: gt, eq
  Register #(.width(1)) u_ZF (.D(main_1_zf), .en(keepZF_BAF), .Q(ZF), .clk(clk));  // open: clr
  or or_1 (or_1_out, nHALT, comparator_1_lt);
  Register #(.width(1)) u_BAF (.D(main_1_baf), .en(keepZF_BAF), .Q(BAF), .clk(clk));  // open: clr
  and and_1 (clk, clock_1_out, or_1_out);
  not not_1 (HALT, or_1_out);

  // Other names for the same wires on the sheet: dbus[7:0] = out_2; r0[7:0] = out_6; r1[7:0] = out_7; r2[7:0] = out_8;
  //   r3[7:0] = out_9; r4[7:0] = out_10; r5[7:0] = out_11; r6[7:0] = out_12; r7[7:0] = out_13; r8[7:0] = out_14;
  //   r9[7:0] = out_15; r10[7:0] = out_16; r11[7:0] = out_17; r12[7:0] = out_18; r13[7:0] = out_19; r14[7:0] = out_20;
  //   r15[7:0] = out_21; sbus[7:0] = out_5

  // Notes on the sheet:
  //   VLD -  01, Rd (xx)
  //   NEG - 02, Rd (xx)
  //   INC - 03, Rd (xx)
  //   DEC - 04, Rd (xx)
  //   CPMZ - 05, Rd (xx)
  //   INV - 06, Rd (xx)
  //   SHL - 08, Rd (xx)
  //   SHR - 09, Rd (xx)
  //   ROL - 0a, Rd (xx)
  //   ROR - 0b, Rd (xx)
  //   NOT - 0c, Rd (xx)
  //   N1 - 0d, Rd (xx)
  //   N0 - 0e, Rd (xx)
  //   OP3 - 5a, Rd (xx)
  //   ADD - 10, Rd Rs
  //   SUB - 11, Rd Rs
  //   MUL - 12, Rd Rs
  //   DIV - 13, Rd Rs
  //   XOR - 1c, Rd Rs
  //   AND - 1d, Rd Rs
  //   OR - 1e, Rd Rs
  //   OP1 - 58, Rd Rs
  //   OP2 - 59, Rd Rs
  //   OP4 - 5b, Rd Rs
  //   OPCODES:
  //   RAM
  //   NOP - 80
  //   JZ - 89, immed
  //   JNZ- 8a, immed
  //   JBAF - 8b, immed
  //   JNBAF - 8c, immed
  //   JMP - 8d, immed
  //   LW - 98, Rd(xx),  immed
  //   SW - 99, Rd(xx), immed
  //   LI - 9a, Rd(xx), immed
  //   LW - 94, Rd(Rs)
  //   SW - 95, Rd(Rs)
  //   MOV - 96, Rd(Rs)
  //   push PC - a0
  //   pop PC- a1
  //   push Rd - b0, Rd (xx)
  //   pop Rd - b1, Rd (xx)
  //   inc SP - c0
  //   dec SP - c1
  //   IMMED
  //   IR-Code
  //   IR-Regs
endmodule

// Regs
module Register_File (
  input  dwrite,
  input  [3:0] dregsel,
  input  [7:0] in_3,
  input  [3:0] sregsel,
  output [7:0] R0,
  output [7:0] R1,
  output [7:0] dbus,
  output [7:0] R2,
  output [7:0] R3,
  output [7:0] R4,
  output [7:0] R5,
  output [7:0] R6,
  output [7:0] R7,
  output [7:0] R8,
  output [7:0] R9,
  output [7:0] R10,
  output [7:0] R11,
  output [7:0] R12,
  output [7:0] R13,
  output [7:0] sbus,
  output [7:0] R14,
  output [7:0] R15
);

  wire clock_1_out, demultiplexer_1_out0, demultiplexer_1_out1, demultiplexer_1_out2, demultiplexer_1_out3,
       demultiplexer_1_out4, demultiplexer_1_out5, demultiplexer_1_out6, demultiplexer_1_out7,
       demultiplexer_1_out8, demultiplexer_1_out9, demultiplexer_1_out10, demultiplexer_1_out11,
       demultiplexer_1_out12, demultiplexer_1_out13, demultiplexer_1_out14, demultiplexer_1_out15;

  Demultiplexer #(.select(4)) demultiplexer_1 (
    .out0(demultiplexer_1_out0), .out1(demultiplexer_1_out1), .out2(demultiplexer_1_out2),
    .out3(demultiplexer_1_out3), .out4(demultiplexer_1_out4), .out5(demultiplexer_1_out5),
    .out6(demultiplexer_1_out6), .out7(demultiplexer_1_out7), .out8(demultiplexer_1_out8),
    .out9(demultiplexer_1_out9), .out10(demultiplexer_1_out10), .out11(demultiplexer_1_out11),
    .out12(demultiplexer_1_out12), .out13(demultiplexer_1_out13), .out14(demultiplexer_1_out14),
    .out15(demultiplexer_1_out15), .in(dwrite), .sel(dregsel));  // open: en
  Clock clock_1 (.out(clock_1_out));
  Register register_1 (.D(in_3), .en(demultiplexer_1_out0), .Q(R0), .clk(clock_1_out));  // open: clr
  Register register_2 (.D(in_3), .en(demultiplexer_1_out1), .Q(R1), .clk(clock_1_out));  // open: clr
  Register register_3 (.D(in_3), .en(demultiplexer_1_out2), .Q(R2), .clk(clock_1_out));  // open: clr
  Register register_4 (.D(in_3), .en(demultiplexer_1_out3), .Q(R3), .clk(clock_1_out));  // open: clr
  Register register_5 (.D(in_3), .en(demultiplexer_1_out4), .Q(R4), .clk(clock_1_out));  // open: clr
  Register register_6 (.D(in_3), .en(demultiplexer_1_out5), .Q(R5), .clk(clock_1_out));  // open: clr
  Register register_7 (.D(in_3), .en(demultiplexer_1_out6), .Q(R6), .clk(clock_1_out));  // open: clr
  Register register_8 (.D(in_3), .en(demultiplexer_1_out7), .Q(R7), .clk(clock_1_out));  // open: clr
  Register register_9 (.D(in_3), .en(demultiplexer_1_out8), .Q(R8), .clk(clock_1_out));  // open: clr
  Register register_10 (.D(in_3), .en(demultiplexer_1_out9), .Q(R9), .clk(clock_1_out));  // open: clr
  Register register_11 (.D(in_3), .en(demultiplexer_1_out10), .Q(R10), .clk(clock_1_out));  // open: clr
  Register register_12 (.D(in_3), .en(demultiplexer_1_out11), .Q(R11), .clk(clock_1_out));  // open: clr
  Register register_13 (.D(in_3), .en(demultiplexer_1_out12), .Q(R12), .clk(clock_1_out));  // open: clr
  Register register_14 (.D(in_3), .en(demultiplexer_1_out13), .Q(R13), .clk(clock_1_out));  // open: clr
  Register register_15 (.D(in_3), .en(demultiplexer_1_out14), .Q(R14), .clk(clock_1_out));  // open: clr
  Register register_16 (.D(in_3), .en(demultiplexer_1_out15), .Q(R15), .clk(clock_1_out));  // open: clr
  Multiplexer #(.select(4), .width(8)) multiplexer_1 (
    .in0(R0), .in1(R1), .in2(R2), .in3(R3), .in4(R4), .in5(R5), .in6(R6), .in7(R7), .in8(R8), .in9(R9),
    .in10(R10), .in11(R11), .in12(R12), .in13(R13), .in14(R14), .in15(R15), .out(dbus), .sel(dregsel));  // open: en
  Multiplexer #(.select(4), .width(8)) multiplexer_2 (
    .in0(R0), .in1(R1), .in2(R2), .in3(R3), .in4(R4), .in5(R5), .in6(R6), .in7(R7), .in8(R8), .in9(R9),
    .in10(R10), .in11(R11), .in12(R12), .in13(R13), .in14(R14), .in15(R15), .out(sbus), .sel(sregsel));  // open: en

  // Other names for the same wires on the sheet: drs[3:0] = dregsel

  // Notes on the sheet:
  //   dval
endmodule

// +PC
module PC_Adder (
  input  [7:0] in_1,
  output [7:0] out_2
);

  Adder adder_1 (.a(in_1), .b(8'h1), .out(out_2), .cin(1'b0));  // open: cout

  // Notes on the sheet:
  //   PC adder
endmodule

// Decoder
module Decoder_Logic (
  input  ZF,
  input  BAF,
  input  [7:0] in_3,
  input  [7:0] in_4,
  output [3:0] dregsel,
  output [3:0] sregsel,
  output [7:0] out_7,
  output out_8,
  output out_9,
  output out_10,
  output out_11,
  output out_12,
  output out_13,
  output out_14,
  output [1:0] out_15,
  output out_16,
  output [1:0] out_17,
  output out_18,
  output out_19,
  output out_20,
  output out_21
);

  wire and_1_out, and_2_out, and_3_out, and_4_out, and_5_out, and_6_out, clock_1_out, multiplexer_4_out,
       multiplexer_6_out, multiplexer_18_out, multiplexer_19_out, multiplexer_21_out, multiplexer_23_out,
       multiplexer_24_out, multiplexer_25_out, multiplexer_29_out, multiplexer_30_out, multiplexer_31_out,
       multiplexer_32_out, multiplexer_34_out, not_1_out, not_2_out, not_3_out, not_4_out, not_5_out,
       not_6_out, not_7_out, not_8_out, or_1_out, or_2_out;
  wire [1:0] multiplexer_1_out, multiplexer_3_out, multiplexer_5_out, multiplexer_7_out, multiplexer_8_out,
       multiplexer_12_out, multiplexer_13_out, multiplexer_15_out, multiplexer_16_out, phase;

  Multiplexer #(.select(3), .width(2), .enable("false")) multiplexer_1 (
    .in0(2'b01), .in1(2'b01), .in2(2'b00), .in3(2'b00), .in4(2'b10), .in5(2'b10), .in6(2'b00), .in7(2'b00),
    .out(multiplexer_1_out), .sel(in_3[2:0]));
  Multiplexer #(.select(2), .enable("false")) multiplexer_2 (
    .in0(1'b1), .in1(1'b0), .in2(1'b0), .in3(1'b0), .out(out_8), .sel(phase));
  not not_1 (not_1_out, in_3[0]);
  Multiplexer #(.select(3), .width(2), .enable("false")) multiplexer_3 (
    .in0(2'b10), .in1(2'b00), .in2(2'b10), .in3(2'b01), .in4(2'b10), .in5(2'b00), .in6(2'b00), .in7(2'b00),
    .out(multiplexer_3_out), .sel(in_3[3:1]));
  Multiplexer #(.select(3), .enable("false")) multiplexer_4 (
    .in0(1'b0), .in1(in_3[0]), .in2(not_1_out), .in3(not_1_out), .in4(1'b0), .in5(1'b0), .in6(1'b0),
    .in7(1'b0), .out(multiplexer_4_out), .sel(in_3[6:4]));
  Multiplexer #(.width(2), .enable("false")) multiplexer_5 (
    .in0(2'b11), .in1(2'b00), .out(multiplexer_5_out), .sel(in_3[0]));
  not not_2 (not_2_out, in_3[7]);
  Multiplexer #(.enable("false")) multiplexer_6 (
    .in0(1'b0), .in1(multiplexer_4_out), .out(multiplexer_6_out), .sel(in_3[7]));
  Multiplexer #(.width(2), .enable("false")) multiplexer_7 (
    .in0(2'b00), .in1(2'b11), .out(multiplexer_7_out), .sel(in_3[0]));
  Multiplexer #(.width(2), .enable("false")) multiplexer_8 (
    .in0(2'b11), .in1(multiplexer_3_out), .out(multiplexer_8_out), .sel(in_3[7]));
  Multiplexer #(.select(2), .enable("false")) multiplexer_9 (
    .in0(1'b0), .in1(1'b0), .in2(1'b0), .in3(not_2_out), .out(out_20), .sel(phase));
  and and_1 (and_1_out, in_3[4], in_3[7]);
  not not_3 (not_3_out, in_3[7]);
  Multiplexer #(.select(2), .enable("false")) multiplexer_10 (
    .in0(1'b0), .in1(1'b0), .in2(1'b0), .in3(multiplexer_6_out), .out(out_11), .sel(phase));
  Multiplexer #(.select(2), .width(2), .enable("false")) multiplexer_11 (
    .in0(2'b00), .in1(2'b00), .in2(2'b00), .in3(multiplexer_8_out), .out(out_17), .sel(phase));
  or or_1 (or_1_out, and_1_out, not_3_out);
  Multiplexer #(.select(3), .width(2), .enable("false")) multiplexer_12 (
    .in0(2'b00), .in1(2'b00), .in2(multiplexer_7_out), .in3(2'b00), .in4(2'b00), .in5(2'b00), .in6(2'b00),
    .in7(2'b00), .out(multiplexer_12_out), .sel(in_3[6:4]));
  Multiplexer #(.select(3), .width(2), .enable("false")) multiplexer_13 (
    .in0(2'b00), .in1(multiplexer_1_out), .in2(multiplexer_5_out), .in3(2'b11), .in4(2'b00), .in5(2'b00),
    .in6(2'b00), .in7(2'b00), .out(multiplexer_13_out), .sel(in_3[6:4]));
  Multiplexer #(.select(2), .enable("false")) multiplexer_14 (
    .in0(1'b0), .in1(or_1_out), .in2(1'b0), .in3(1'b0), .out(out_9), .sel(phase));
  Multiplexer #(.width(2), .enable("false")) multiplexer_15 (
    .in0(2'b00), .in1(multiplexer_12_out), .out(multiplexer_15_out), .sel(in_3[7]));
  Multiplexer #(.width(2), .enable("false")) multiplexer_16 (
    .in0(2'b00), .in1(multiplexer_13_out), .out(multiplexer_16_out), .sel(in_3[7]));
  Multiplexer #(.select(2), .width(2), .enable("false")) multiplexer_17 (
    .in0(2'b00), .in1(2'b00), .in2(multiplexer_15_out), .in3(multiplexer_16_out), .out(out_15), .sel(phase));
  not not_4 (not_4_out, ZF);
  not not_5 (not_5_out, BAF);
  and and_2 (and_2_out, in_3[7], in_3[3]);
  not not_6 (not_6_out, in_3[4]);
  Multiplexer #(.select(3), .enable("false")) multiplexer_18 (
    .in0(1'b0), .in1(ZF), .in2(not_4_out), .in3(BAF), .in4(not_5_out), .in5(1'b1), .in6(1'b0), .in7(1'b0),
    .out(multiplexer_18_out), .sel(in_3[2:0]));
  and and_3 (and_3_out, in_3[7], in_3[6]);
  Counter #(.width(2), .max('h3)) counter_1 (.Q(phase), .clk(clock_1_out));  // open: load, D, count, carry, clr
  Clock clock_1 (.out(clock_1_out));
  and and_4 (and_4_out, in_3[5], in_3[7], in_3[0], not_6_out);
  Multiplexer #(.select(3), .enable("false")) multiplexer_19 (
    .in0(1'b1), .in1(1'b0), .in2(1'b1), .in3(1'b0), .in4(1'b1), .in5(1'b0), .in6(1'b1), .in7(1'b0),
    .out(multiplexer_19_out), .sel(in_3[2:0]));
  Multiplexer #(.select(2), .enable("false")) multiplexer_20 (
    .in0(1'b0), .in1(1'b0), .in2(1'b0), .in3(and_3_out), .out(out_18), .sel(phase));
  ROM #(.dataWidth(1)) rom_1 (.addr(in_3), .data(out_21));  // open: sel
  or or_2 (or_2_out, and_2_out, and_4_out);
  Multiplexer #(.select(3), .enable("false")) multiplexer_21 (
    .in0(multiplexer_18_out), .in1(1'b0), .in2(in_3[0]), .in3(1'b0), .in4(1'b0), .in5(1'b0), .in6(1'b0),
    .in7(1'b0), .out(multiplexer_21_out), .sel(in_3[6:4]));
  Multiplexer #(.select(2), .enable("false")) multiplexer_22 (
    .in0(1'b0), .in1(1'b0), .in2(or_2_out), .in3(1'b0), .out(out_10), .sel(phase));
  and and_5 (and_5_out, in_3[7], in_3[3]);
  Multiplexer #(.enable("false")) multiplexer_23 (
    .in0(1'b0), .in1(multiplexer_21_out), .out(multiplexer_23_out), .sel(in_3[7]));
  Multiplexer #(.select(3), .enable("false")) multiplexer_24 (
    .in0(1'b0), .in1(multiplexer_19_out), .in2(1'b0), .in3(in_3[0]), .in4(1'b0), .in5(1'b0), .in6(1'b0),
    .in7(1'b0), .out(multiplexer_24_out), .sel(in_3[6:4]));
  Multiplexer #(.enable("false")) multiplexer_25 (
    .in0(1'b1), .in1(multiplexer_24_out), .out(multiplexer_25_out), .sel(in_3[7]));
  Multiplexer #(.select(2), .enable("false")) multiplexer_26 (
    .in0(1'b1), .in1(out_9), .in2(and_5_out), .in3(multiplexer_23_out), .out(out_12), .sel(phase));
  Multiplexer #(.select(2), .enable("false")) multiplexer_27 (
    .in0(1'b0), .in1(1'b0), .in2(1'b0), .in3(multiplexer_25_out), .out(out_14), .sel(phase));
  and and_6 (and_6_out, in_3[7], in_3[6], in_3[0]);
  Multiplexer #(.select(2), .enable("false")) multiplexer_28 (
    .in0(1'b0), .in1(1'b0), .in2(1'b0), .in3(and_6_out), .out(out_19), .sel(phase));
  not not_7 (not_7_out, ZF);
  not not_8 (not_8_out, BAF);
  Multiplexer #(.select(3), .enable("false")) multiplexer_29 (
    .in0(1'b0), .in1(not_7_out), .in2(ZF), .in3(not_8_out), .in4(BAF), .in5(1'b0), .in6(1'b1), .in7(1'b1),
    .out(multiplexer_29_out), .sel(in_3[2:0]));
  Multiplexer #(.enable("false")) multiplexer_30 (.in0(1'b1), .in1(1'b0), .out(multiplexer_30_out), .sel(in_3[0]));
  Multiplexer #(.select(3), .enable("false")) multiplexer_31 (
    .in0(1'b0), .in1(1'b0), .in2(1'b1), .in3(1'b0), .in4(1'b0), .in5(1'b0), .in6(1'b0), .in7(1'b0),
    .out(multiplexer_31_out), .sel(in_3[6:4]));
  Multiplexer #(.select(3), .enable("false")) multiplexer_32 (
    .in0(multiplexer_29_out), .in1(1'b1), .in2(multiplexer_30_out), .in3(1'b1), .in4(1'b1), .in5(1'b1),
    .in6(1'b1), .in7(1'b1), .out(multiplexer_32_out), .sel(in_3[6:4]));
  Multiplexer #(.select(2), .enable("false")) multiplexer_33 (
    .in0(1'b0), .in1(1'b0), .in2(1'b0), .in3(multiplexer_31_out), .out(out_16), .sel(phase));
  Multiplexer #(.enable("false")) multiplexer_34 (
    .in0(1'b1), .in1(multiplexer_32_out), .out(multiplexer_34_out), .sel(in_3[7]));
  Multiplexer #(.select(2), .enable("false")) multiplexer_35 (
    .in0(1'b1), .in1(1'b1), .in2(1'b1), .in3(multiplexer_34_out), .out(out_13), .sel(phase));

  assign dregsel = in_4[7:4];
  assign out_7 = in_3;
  assign sregsel = in_4[3:0];

  // Other names for the same wires on the sheet: aluop[7:0] = in_3; irbit7 = in_3[7]; Imload = out_10;
  //   IRRload = out_9; irbit4 = in_3[4]; OP1[2:0] = in_3[6:4]; irbit5 = in_3[5]; irbit6 = in_3[6]; irbit0 = in_3[0];
  //   OP2[3:0] = in_3[3:0]; irbit1 = in_3[1]; irbit2 = in_3[2]; irbit3 = in_3[3]; rd[3:0] = in_4[7:4];
  //   rs[3:0] = in_4[3:0]

  // Notes on the sheet:
  //   IRCload
  //   IRCode
  //   Read/write
  //   Keep ZF/BAF
  //   regsel
  //   IRRegs
  //   IRRload
  //   Adrsel
  //   aluop
  //   SP en
  //   ¬HALT
  //   Phase Counter:
  //   contents of rom_1 (hex, n*v repeats v):
  //   0 6*1 0 7*1 0 4*1 8*0 1 1 1 57*0 4*1 36*0 1 8*0 5*1 6*0 1 1 1 0 1 1 1 5*0 1 1 14*0 1 1 14*0 1 1
  //   Imload
  //   PCload
  //   dwrite
  //   SP sub
  //   PCselect
  //   dload
endmodule

// +/-SP
module SP_adder_subtractor (
  input  [7:0] in_1,
  input  in_2,
  output [7:0] out_3
);

  wire [7:0] adder_1_out, subtractor_1_out;

  Adder adder_1 (.a(in_1), .b(8'h1), .out(adder_1_out), .cin(1'b0));  // open: cout
  Subtractor subtractor_1 (.a(in_1), .b(8'h1), .out(subtractor_1_out));  // open: bin, bout
  Multiplexer #(.width(8), .enable("false")) multiplexer_1 (
    .in0(adder_1_out), .in1(subtractor_1_out), .out(out_3), .sel(in_2));
endmodule
